// Logisim project Calculadora_4bits.circ as structural Verilog: 14 circuits, main circuit Full-Adder
module main (
  input  [3:0] A,
  input  [3:0] B,
  input  [1:0] in_3,
  output [7:0] \Saída_em_Binário 
);

  wire comparador_1_sled, displaycentena_1_a, displaycentena_1_b, displaycentena_1_c, displaycentena_1_d,
       displaycentena_1_e, displaycentena_1_f, displaycentena_1_g, displaydezena_1_a, displaydezena_1_b,
       displaydezena_1_c, displaydezena_1_d, displaydezena_1_e, displaydezena_1_f, displaydezena_1_g,
       displaydezena_2_a, displaydezena_2_b, displaydezena_2_c, displaydezena_2_d, displaydezena_2_e,
       displaydezena_2_f, displaydezena_2_g, displaydezena_3_a, displaydezena_3_b, displaydezena_3_c,
       displaydezena_3_d, displaydezena_3_e, displaydezena_3_f, displaydezena_3_g, displayunidade_1_a,
       displayunidade_1_b, displayunidade_1_c, displayunidade_1_d, displayunidade_1_e, displayunidade_1_f,
       displayunidade_1_g, displayunidade_2_a, displayunidade_2_b, displayunidade_2_c, displayunidade_2_d,
       displayunidade_2_e, displayunidade_2_f, displayunidade_2_g, displayunidade_3_a, displayunidade_3_b,
       displayunidade_3_c, displayunidade_3_d, displayunidade_3_e, displayunidade_3_f, displayunidade_3_g;
  wire [7:0] bit_extender_1_out, bit_extender_2_out;

  assign bit_extender_1_out = {{4{1'b0}}, A};  // Bit_Extender bit_extender_1
  assign bit_extender_2_out = {{4{1'b0}}, B};  // Bit_Extender bit_extender_2
  Comparador comparador_1 (.Chave_seletora(in_3), .Entrada_B(B), .sLed(comparador_1_sled));
  LED E (.in(comparador_1_sled));
  DisplayDezena displaydezena_1 (
    .A7(bit_extender_1_out[7]), .A6(bit_extender_1_out[6]), .A5(bit_extender_1_out[5]),
    .A4(bit_extender_1_out[4]), .A3(bit_extender_1_out[3]), .A2(bit_extender_1_out[2]),
    .A1(bit_extender_1_out[1]), .A0(bit_extender_1_out[0]), .A(displaydezena_1_a), .B(displaydezena_1_b),
    .C(displaydezena_1_c), .D(displaydezena_1_d), .E(displaydezena_1_e), .F(displaydezena_1_f),
    .G(displaydezena_1_g));
  DisplayUnidade displayunidade_1 (
    .A7(bit_extender_1_out[7]), .A6(bit_extender_1_out[6]), .A5(bit_extender_1_out[5]),
    .A4(bit_extender_1_out[4]), .A3(bit_extender_1_out[3]), .A2(bit_extender_1_out[2]),
    .A1(bit_extender_1_out[1]), .A0(bit_extender_1_out[0]), .A(displayunidade_1_a), .B(displayunidade_1_b),
    .C(displayunidade_1_c), .D(displayunidade_1_d), .E(displayunidade_1_e), .F(displayunidade_1_f),
    .G(displayunidade_1_g));
  ULA ula_1 (.A(A), .B(B), .in_3(in_3), .out_4(\Saída_em_Binário ));
  DisplayDezena displaydezena_2 (
    .A7(bit_extender_2_out[7]), .A6(bit_extender_2_out[6]), .A5(bit_extender_2_out[5]),
    .A4(bit_extender_2_out[4]), .A3(bit_extender_2_out[3]), .A2(bit_extender_2_out[2]),
    .A1(bit_extender_2_out[1]), .A0(bit_extender_2_out[0]), .A(displaydezena_2_a), .B(displaydezena_2_b),
    .C(displaydezena_2_c), .D(displaydezena_2_d), .E(displaydezena_2_e), .F(displaydezena_2_f),
    .G(displaydezena_2_g));
  DisplayUnidade displayunidade_2 (
    .A7(bit_extender_2_out[7]), .A6(bit_extender_2_out[6]), .A5(bit_extender_2_out[5]),
    .A4(bit_extender_2_out[4]), .A3(bit_extender_2_out[3]), .A2(bit_extender_2_out[2]),
    .A1(bit_extender_2_out[1]), .A0(bit_extender_2_out[0]), .A(displayunidade_2_a), .B(displayunidade_2_b),
    .C(displayunidade_2_c), .D(displayunidade_2_d), .E(displayunidade_2_e), .F(displayunidade_2_f),
    .G(displayunidade_2_g));
  _7_Segment_Display u_7_segment_display_1 (
    .g(displaydezena_1_g), .f(displaydezena_1_f), .a(displaydezena_1_a), .b(displaydezena_1_b),
    .e(displaydezena_1_e), .d(displaydezena_1_d), .c(displaydezena_1_c));  // open: dp
  _7_Segment_Display u_7_segment_display_2 (
    .g(displayunidade_1_g), .f(displayunidade_1_f), .a(displayunidade_1_a), .b(displayunidade_1_b),
    .e(displayunidade_1_e), .d(displayunidade_1_d), .c(displayunidade_1_c));  // open: dp
  _7_Segment_Display u_7_segment_display_3 (
    .g(displaydezena_2_g), .f(displaydezena_2_f), .a(displaydezena_2_a), .b(displaydezena_2_b),
    .e(displaydezena_2_e), .d(displaydezena_2_d), .c(displaydezena_2_c));  // open: dp
  _7_Segment_Display u_7_segment_display_4 (
    .g(displayunidade_2_g), .f(displayunidade_2_f), .a(displayunidade_2_a), .b(displayunidade_2_b),
    .e(displayunidade_2_e), .d(displayunidade_2_d), .c(displayunidade_2_c));  // open: dp
  DisplayDezena displaydezena_3 (
    .A7(\Saída_em_Binário [7]), .A6(\Saída_em_Binário [6]), .A5(\Saída_em_Binário [5]),
    .A4(\Saída_em_Binário [4]), .A3(\Saída_em_Binário [3]), .A2(\Saída_em_Binário [2]),
    .A1(\Saída_em_Binário [1]), .A0(\Saída_em_Binário [0]), .A(displaydezena_3_a), .B(displaydezena_3_b),
    .C(displaydezena_3_c), .D(displaydezena_3_d), .E(displaydezena_3_e), .F(displaydezena_3_f),
    .G(displaydezena_3_g));
  DisplayUnidade displayunidade_3 (
    .A7(\Saída_em_Binário [7]), .A6(\Saída_em_Binário [6]), .A5(\Saída_em_Binário [5]),
    .A4(\Saída_em_Binário [4]), .A3(\Saída_em_Binário [3]), .A2(\Saída_em_Binário [2]),
    .A1(\Saída_em_Binário [1]), .A0(\Saída_em_Binário [0]), .A(displayunidade_3_a), .B(displayunidade_3_b),
    .C(displayunidade_3_c), .D(displayunidade_3_d), .E(displayunidade_3_e), .F(displayunidade_3_f),
    .G(displayunidade_3_g));
  DisplayCentena displaycentena_1 (
    .A7(\Saída_em_Binário [7]), .A6(\Saída_em_Binário [6]), .A5(\Saída_em_Binário [5]),
    .A4(\Saída_em_Binário [4]), .A3(\Saída_em_Binário [3]), .A2(\Saída_em_Binário [2]),
    .A1(\Saída_em_Binário [1]), .A0(\Saída_em_Binário [0]), .A(displaycentena_1_a), .B(displaycentena_1_b),
    .C(displaycentena_1_c), .D(displaycentena_1_d), .E(displaycentena_1_e), .F(displaycentena_1_f),
    .G(displaycentena_1_g));
  _7_Segment_Display u_7_segment_display_5 (
    .g(displaycentena_1_g), .f(displaycentena_1_f), .a(displaycentena_1_a), .b(displaycentena_1_b),
    .e(displaycentena_1_e), .d(displaycentena_1_d), .c(displaycentena_1_c));  // open: dp
  _7_Segment_Display u_7_segment_display_6 (
    .g(displaydezena_3_g), .f(displaydezena_3_f), .a(displaydezena_3_a), .b(displaydezena_3_b),
    .e(displaydezena_3_e), .d(displaydezena_3_d), .c(displaydezena_3_c));  // open: dp
  _7_Segment_Display u_7_segment_display_7 (
    .g(displayunidade_3_g), .f(displayunidade_3_f), .a(displayunidade_3_a), .b(displayunidade_3_b),
    .e(displayunidade_3_e), .d(displayunidade_3_d), .c(displayunidade_3_c));  // open: dp

  // Notes on the sheet:
  //   CALCULADORA 4 BITS
  //   ENTRADAS
  //   Erro se divisão por zero
  //   0 0 - Soma
  //   0 1 - Subtração
  //   10 - Multiplicação
  //   11 - Divisão
  //   Chave Seletora
  //   ENTRADA A EM DECIMAL
  //   ENTRADA B EM DECIMAL
  //   SAÍDA EM DECIMAL
endmodule

// Somador Completo
module Full_Adder (
  input  A,
  input  B,
  input  Cin,
  output Soma0,
  output Cout
);

  wire and_1_out, and_2_out, and_3_out, xor_1_out;

  xor xor_1 (xor_1_out, A, B);
  and and_1 (and_1_out, B, Cin);
  and and_2 (and_2_out, A, Cin);
  and and_3 (and_3_out, A, B);
  xor xor_2 (Soma0, xor_1_out, Cin);
  or u_Cout (Cout, and_1_out, and_2_out, and_3_out);

  // Notes on the sheet:
  //   Somador Bit-Bit
endmodule

module Full_Subtrator (
  input  A,
  input  B,
  input  Bin,
  output Sub,
  output Bout
);

  wire and_1_out, and_2_out, and_3_out, xor_1_out;

  xor xor_1 (xor_1_out, A, B);
  and and_1 (and_1_out, ~A, Bin);  // AND_Gate
  and and_2 (and_2_out, ~A, B);  // AND_Gate
  and and_3 (and_3_out, B, Bin);
  xor xor_2 (Sub, xor_1_out, Bin);
  or u_Bout (Bout, and_1_out, and_2_out, and_3_out);

  // Notes on the sheet:
  //   Subtrador Bit-Bit
endmodule

module Adder_4_bits (
  input  [3:0] A,
  input  [3:0] B,
  output [4:0] S,
  output Cout
);

  wire full_adder_2_cout, full_adder_3_cout, full_adder_4_cout;

  Full_Adder full_adder_1 (.A(A[3]), .B(B[3]), .Cin(full_adder_2_cout), .Cout(Cout), .Soma0(S[3]));
  Full_Adder full_adder_2 (.A(A[2]), .B(B[2]), .Cin(full_adder_3_cout), .Cout(full_adder_2_cout), .Soma0(S[2]));
  Full_Adder full_adder_3 (.A(A[1]), .B(B[1]), .Cin(full_adder_4_cout), .Cout(full_adder_3_cout), .Soma0(S[1]));
  Full_Adder full_adder_4 (.A(A[0]), .B(B[0]), .Cin(1'b0), .Cout(full_adder_4_cout), .Soma0(S[0]));

  assign S[4] = Cout;

  // Notes on the sheet:
  //   Somador com 4 bits
endmodule

module Subtrator_4_bits (
  input  [3:0] A,
  input  [3:0] B,
  output [4:0] out_3,
  output Bout
);

  wire full_subtrator_2_bout, full_subtrator_3_bout, full_subtrator_4_bout;

  Full_Subtrator full_subtrator_1 (.Sub(out_3[3]), .Bout(Bout), .A(A[3]), .B(B[3]), .Bin(full_subtrator_2_bout));
  Full_Subtrator full_subtrator_2 (
    .Sub(out_3[2]), .Bout(full_subtrator_2_bout), .A(A[2]), .B(B[2]), .Bin(full_subtrator_3_bout));
  Full_Subtrator full_subtrator_3 (
    .Sub(out_3[1]), .Bout(full_subtrator_3_bout), .A(A[1]), .B(B[1]), .Bin(full_subtrator_4_bout));
  Full_Subtrator full_subtrator_4 (.Sub(out_3[0]), .Bout(full_subtrator_4_bout), .A(A[0]), .B(B[0]), .Bin(1'b0));

  assign out_3[4] = Bout;

  // Notes on the sheet:
  //   Subtrador com 4 bits
endmodule

module Multiplication_4_bits (
  input  [3:0] A,
  input  [3:0] B,
  output [7:0] out_3
);

  wire [2:0] B0A1_out;
  wire [3:0] B1A0_out, B2A0_out, B3A0_out;
  wire [4:1] Somador_2_s, Somador_s;

  and B3A3 (B3A0_out[3], B[3], A[3]);
  and B1A3 (B1A0_out[3], B[1], A[3]);
  and B2A3 (B2A0_out[3], B[2], A[3]);
  and B2A2 (B2A0_out[2], B[2], A[2]);
  and B3A1 (B3A0_out[1], B[3], A[1]);
  and B3A2 (B3A0_out[2], B[3], A[2]);
  and B0A3 (B0A1_out[2], B[0], A[3]);
  and B1A2 (B1A0_out[2], B[1], A[2]);
  and B2A1 (B2A0_out[1], B[2], A[1]);
  and B3A0 (B3A0_out[0], B[3], A[0]);
  and B0A2 (B0A1_out[1], B[0], A[2]);
  and B1A1 (B1A0_out[1], B[1], A[1]);
  and B2A0 (B2A0_out[0], B[2], A[0]);
  and B0A1 (B0A1_out[0], B[0], A[1]);
  and B0A0 (out_3[0], B[0], A[0]);
  and B1A0 (B1A0_out[0], B[1], A[0]);
  Adder_4_bits Somador (.A({1'b0, B0A1_out}), .B(B1A0_out), .S({Somador_s, out_3[1]}));  // open: Cout
  Adder_4_bits Somador_2 (.A(Somador_s), .B(B2A0_out), .S({Somador_2_s, out_3[2]}));  // open: Cout
  Adder_4_bits Somador_3 (.A(Somador_2_s), .B(B3A0_out), .S(out_3[7:3]));  // open: Cout

  // Notes on the sheet:
  //   Multiplicador com 4 bits
endmodule

module _2_Bits_Division (
  input  [1:0] A,
  input  [1:0] B,
  output [1:0] out_3,
  output E
);

  wire and_2_out, and_3_out, and_4_out, not_1_out, not_2_out, not_3_out;

  not not_1 (not_1_out, B[1]);
  not not_2 (not_2_out, B[1]);
  not not_3 (not_3_out, B[0]);
  and and_1 (out_3[1], not_1_out, B[0], A[1]);
  and and_2 (and_2_out, A[0], not_2_out, B[0]);
  and and_3 (and_3_out, A[1], B[1], not_3_out);
  and and_4 (and_4_out, A[1], A[0]);
  and and_5 (E, ~B[1], ~B[0]);  // AND_Gate
  or or_1 (out_3[0], and_2_out, and_3_out, and_4_out);

  // Notes on the sheet:
  //   Divisor de 2 bits
endmodule

module ULA (
  input  [3:0] A,
  input  [3:0] B,
  input  [1:0] in_3,
  output [7:0] out_4
);

  wire [3:0] divider_1_out;
  wire [4:0] adder_4_bits_1_s, subtrator_4_bits_1_out_3;
  wire [7:0] bit_extender_1_out, bit_extender_2_out, bit_extender_3_out, multiplication_4_bits_1_out_3;

  Divider #(.width(4)) divider_1 (.a(A), .b(B), .out(divider_1_out));  // open: upper, rem
  Adder_4_bits adder_4_bits_1 (.A(A), .B(B), .S(adder_4_bits_1_s));  // open: Cout
  Subtrator_4_bits subtrator_4_bits_1 (.A(A), .B(B), .out_3(subtrator_4_bits_1_out_3));  // open: Bout
  Multiplication_4_bits multiplication_4_bits_1 (.A(A), .B(B), .out_3(multiplication_4_bits_1_out_3));
  assign bit_extender_1_out = {{3{1'b0}}, adder_4_bits_1_s};  // Bit_Extender bit_extender_1
  assign bit_extender_2_out = {{3{1'b0}}, subtrator_4_bits_1_out_3};  // Bit_Extender bit_extender_2
  assign bit_extender_3_out = {{4{1'b0}}, divider_1_out};  // Bit_Extender bit_extender_3
  Mux_4x1___8bits mux_4x1_8bits_1 (
    .in_1(bit_extender_1_out), .in_2(bit_extender_2_out), .in_3(multiplication_4_bits_1_out_3),
    .in_4(bit_extender_3_out), .out_6(out_4), .in_5(in_3));

  // Notes on the sheet:
  //   ENTRADAS
  //   UNIDADE LÓGICA ARITMETICA (ULA)
  //   CHAVE SELETORA
endmodule
module DisplayUnidade (
  input  A7,
  input  A6,
  input  A5,
  input  A4,
  input  A3,
  input  A2,
  input  A1,
  input  A0,
  output A,
  output B,
  output C,
  output D,
  output E,
  output F,
  output G
);

  wire and_1_out, and_2_out, and_3_out, and_4_out, and_5_out, and_6_out, and_7_out, and_8_out, and_9_out,
       and_10_out, and_11_out, and_12_out, and_13_out, and_14_out, and_15_out, and_16_out, and_17_out,
       and_18_out, and_19_out, and_20_out, and_21_out, and_22_out, and_23_out, and_24_out, and_25_out,
       and_26_out, and_27_out, and_28_out, and_29_out, and_30_out, and_31_out, and_32_out, and_33_out,
       and_34_out, and_35_out, and_36_out, and_37_out, and_38_out, and_39_out, and_40_out, and_41_out,
       and_42_out, and_43_out, and_44_out, and_45_out, and_46_out, and_47_out, and_48_out, and_49_out,
       and_50_out, and_51_out, and_52_out, and_53_out, and_54_out, and_55_out, and_56_out, and_57_out,
       and_58_out, and_59_out, and_60_out, and_61_out, and_62_out, and_63_out, and_64_out, and_65_out,
       and_66_out, and_67_out, and_68_out, and_69_out, and_70_out, and_71_out, and_72_out, and_73_out,
       and_74_out, and_75_out, and_76_out, and_77_out, and_78_out, and_79_out, and_80_out, and_81_out,
       and_82_out, and_83_out, and_84_out, and_85_out, and_86_out, and_87_out, and_88_out, and_89_out,
       and_90_out, and_91_out, and_92_out, and_93_out, and_94_out, and_95_out, and_96_out, and_97_out,
       and_98_out, and_99_out, and_100_out, and_101_out, and_102_out, and_103_out, and_104_out, and_105_out,
       and_106_out, and_107_out, and_108_out, and_109_out, and_110_out, and_111_out, and_112_out,
       and_113_out, and_114_out, and_115_out, and_116_out, and_117_out, and_118_out, and_119_out,
       and_120_out, and_121_out, and_122_out, and_123_out, and_124_out, and_125_out, and_126_out,
       and_127_out, and_128_out, and_129_out, and_130_out, and_131_out, and_132_out, and_133_out,
       and_134_out, and_135_out, and_136_out, and_137_out, and_138_out, and_139_out, and_140_out,
       and_141_out, and_142_out, and_143_out, and_144_out, and_145_out, and_146_out, and_147_out,
       and_148_out, and_149_out, and_150_out, and_151_out, and_152_out, and_153_out, and_154_out,
       and_155_out, and_156_out, and_157_out, and_158_out, and_159_out, and_160_out, and_161_out,
       and_162_out, and_163_out, and_164_out, and_165_out, and_166_out, and_167_out, and_168_out,
       and_169_out, and_170_out, and_171_out, and_172_out, and_173_out, and_174_out, and_175_out,
       and_176_out, and_177_out, and_178_out, and_179_out, and_180_out, and_181_out, and_182_out,
       and_183_out, and_184_out, and_185_out, and_186_out, and_187_out, and_188_out, and_189_out,
       and_190_out, and_191_out, and_192_out, and_193_out, and_194_out, and_195_out, and_196_out,
       and_197_out, and_198_out, and_199_out, and_200_out, and_201_out, and_202_out, and_203_out,
       and_204_out, and_205_out, and_206_out, and_207_out, and_208_out, and_209_out, and_210_out,
       and_211_out, and_212_out, and_213_out, and_214_out, and_215_out, and_216_out, and_217_out,
       and_218_out, and_219_out, and_220_out, and_221_out, and_222_out, and_223_out, and_224_out,
       and_225_out, and_226_out, and_227_out, and_228_out, and_229_out, and_230_out, and_231_out,
       and_232_out, and_233_out, and_234_out, and_235_out, and_236_out, and_237_out, and_238_out,
       and_239_out, and_240_out, and_241_out, and_242_out, and_243_out, and_244_out, and_245_out,
       and_246_out, and_247_out, and_248_out, and_249_out, and_250_out, and_251_out, and_252_out,
       and_253_out, and_254_out, and_255_out, and_256_out, and_257_out, and_258_out, and_259_out,
       and_260_out, and_261_out, and_262_out, and_263_out, and_264_out, and_265_out, and_266_out,
       and_267_out, and_268_out, and_269_out, and_270_out, and_271_out, and_272_out, and_273_out,
       and_274_out, and_275_out, and_276_out, and_277_out, and_278_out, and_279_out, and_280_out,
       and_281_out, and_282_out, and_283_out, and_284_out, and_285_out, and_286_out, and_287_out,
       and_288_out, and_289_out, and_290_out, and_291_out, and_292_out, and_293_out, and_294_out,
       and_295_out, and_296_out, and_297_out, and_298_out, and_299_out, and_300_out, and_301_out,
       and_302_out, and_303_out, and_304_out, and_305_out, and_306_out, and_307_out, and_308_out,
       and_309_out, and_310_out, and_311_out, and_312_out, and_313_out, and_314_out, and_315_out,
       and_316_out, and_317_out, and_318_out, and_319_out, and_320_out, and_321_out, and_322_out,
       and_323_out, and_324_out, and_325_out, and_326_out, and_327_out, and_328_out, and_329_out,
       and_330_out, and_331_out, and_332_out, and_333_out, and_334_out, and_335_out, and_336_out,
       and_337_out, and_338_out, and_339_out, and_340_out, and_341_out, and_342_out, and_343_out,
       and_344_out, and_345_out, and_346_out, and_347_out, and_348_out, and_349_out, and_350_out,
       and_351_out, and_352_out, and_353_out, and_354_out, and_355_out, and_356_out, and_357_out,
       and_358_out, and_359_out, and_360_out, and_361_out, and_362_out, and_363_out, and_364_out,
       and_365_out, and_366_out, and_367_out, and_368_out, and_369_out, and_370_out, and_371_out, not_1_out,
       not_2_out, not_3_out, not_4_out, not_5_out, not_6_out, not_7_out, not_8_out, not_9_out, not_10_out,
       not_11_out, not_12_out, not_13_out, not_14_out, not_15_out, not_16_out, not_17_out, not_18_out,
       not_19_out, not_20_out, not_21_out, not_22_out, not_23_out, not_24_out, not_25_out, not_26_out,
       not_27_out, not_28_out, not_29_out, not_30_out, not_31_out, not_32_out, not_33_out, not_34_out,
       not_35_out, not_36_out, not_37_out, not_38_out, not_39_out, not_40_out, not_41_out, not_42_out,
       not_43_out, not_44_out, not_45_out, not_46_out, not_47_out, not_48_out, not_49_out, not_50_out,
       not_51_out, not_52_out, not_53_out, not_54_out, not_55_out, not_56_out, not_57_out, not_58_out,
       not_59_out, not_60_out, not_61_out, not_62_out, not_63_out, not_64_out, not_65_out, not_66_out,
       not_67_out, not_68_out, not_69_out, not_70_out, not_71_out, not_72_out, not_73_out, not_74_out,
       not_75_out, not_76_out, not_77_out, not_78_out, not_79_out, not_80_out, not_81_out, not_82_out,
       not_83_out, not_84_out, not_85_out, not_86_out, not_87_out, not_88_out, not_89_out, not_90_out,
       not_91_out, not_92_out, not_93_out, not_94_out, not_95_out, not_96_out, not_97_out, not_98_out,
       not_99_out, not_100_out, not_101_out, not_102_out, not_103_out, not_104_out, not_105_out, not_106_out,
       not_107_out, not_108_out, not_109_out, not_110_out, not_111_out, not_112_out, not_113_out,
       not_114_out, not_115_out, not_116_out, not_117_out, not_118_out, not_119_out, not_120_out,
       not_121_out, not_122_out, not_123_out, not_124_out, not_125_out, not_126_out, not_127_out,
       not_128_out, not_129_out, not_130_out, not_131_out, not_132_out, not_133_out, not_134_out,
       not_135_out, not_136_out, not_137_out, not_138_out, not_139_out, not_140_out, not_141_out,
       not_142_out, not_143_out, not_144_out, not_145_out, not_146_out, not_147_out, not_148_out,
       not_149_out, not_150_out, not_151_out, not_152_out, not_153_out, not_154_out, not_155_out,
       not_156_out, not_157_out, not_158_out, not_159_out, not_160_out, not_161_out, not_162_out,
       not_163_out, not_164_out, not_165_out, not_166_out, not_167_out, not_168_out, not_169_out,
       not_170_out, not_171_out, not_172_out, not_173_out, not_174_out, not_175_out, not_176_out,
       not_177_out, not_178_out, not_179_out, not_180_out, not_181_out, not_182_out, not_183_out,
       not_184_out, not_185_out, not_186_out, not_187_out, not_188_out, not_189_out, not_190_out,
       not_191_out, not_192_out, not_193_out, not_194_out, not_195_out, not_196_out, not_197_out,
       not_198_out, not_199_out, not_200_out, not_201_out, not_202_out, not_203_out, not_204_out,
       not_205_out, not_206_out, not_207_out, not_208_out, not_209_out, not_210_out, not_211_out,
       not_212_out, not_213_out, not_214_out, not_215_out, not_216_out, not_217_out, not_218_out,
       not_219_out, not_220_out, not_221_out, not_222_out, not_223_out, not_224_out, not_225_out,
       not_226_out, not_227_out, not_228_out, not_229_out, not_230_out, not_231_out, not_232_out,
       not_233_out, not_234_out, not_235_out, not_236_out, not_237_out, not_238_out, not_239_out,
       not_240_out, not_241_out, not_242_out, not_243_out, not_244_out, not_245_out, not_246_out,
       not_247_out, not_248_out, not_249_out, not_250_out, not_251_out, not_252_out, not_253_out,
       not_254_out, not_255_out, not_256_out, not_257_out, not_258_out, not_259_out, not_260_out,
       not_261_out, not_262_out, not_263_out, not_264_out, not_265_out, not_266_out, not_267_out,
       not_268_out, not_269_out, not_270_out, not_271_out, not_272_out, not_273_out, not_274_out,
       not_275_out, not_276_out, not_277_out, not_278_out, not_279_out, not_280_out, not_281_out,
       not_282_out, not_283_out, not_284_out, not_285_out, not_286_out, not_287_out, not_288_out,
       not_289_out, not_290_out, not_291_out, not_292_out, not_293_out, not_294_out, not_295_out,
       not_296_out, not_297_out, not_298_out, not_299_out, not_300_out, not_301_out, not_302_out,
       not_303_out, not_304_out, not_305_out, not_306_out, not_307_out, not_308_out, not_309_out,
       not_310_out, not_311_out, not_312_out, not_313_out, not_314_out, not_315_out, not_316_out,
       not_317_out, not_318_out, not_319_out, not_320_out, not_321_out, not_322_out, not_323_out,
       not_324_out, not_325_out, not_326_out, not_327_out, not_328_out, not_329_out, not_330_out,
       not_331_out, not_332_out, not_333_out, not_334_out, not_335_out, not_336_out, not_337_out,
       not_338_out, not_339_out, not_340_out, not_341_out, not_342_out, not_343_out, not_344_out,
       not_345_out, not_346_out, not_347_out, not_348_out, not_349_out, not_350_out, not_351_out,
       not_352_out, not_353_out, not_354_out, not_355_out, not_356_out, not_357_out, not_358_out,
       not_359_out, not_360_out, not_361_out, not_362_out, not_363_out, not_364_out, not_365_out,
       not_366_out, not_367_out, not_368_out, not_369_out, not_370_out, not_371_out, not_372_out,
       not_373_out, not_374_out, not_375_out, not_376_out, not_377_out, not_378_out, not_379_out,
       not_380_out, not_381_out, not_382_out, not_383_out, not_384_out, not_385_out, not_386_out,
       not_387_out, not_388_out, not_389_out, not_390_out, not_391_out, not_392_out, not_393_out,
       not_394_out, not_395_out, not_396_out, not_397_out, not_398_out, not_399_out, not_400_out,
       not_401_out, not_402_out, not_403_out, not_404_out, not_405_out, not_406_out, not_407_out,
       not_408_out, not_409_out, not_410_out, not_411_out, not_412_out, not_413_out, not_414_out,
       not_415_out, not_416_out, not_417_out, not_418_out, not_419_out, not_420_out, not_421_out,
       not_422_out, not_423_out, not_424_out, not_425_out, not_426_out, not_427_out, not_428_out,
       not_429_out, not_430_out, not_431_out, not_432_out, not_433_out, not_434_out, not_435_out,
       not_436_out, not_437_out, not_438_out, not_439_out, not_440_out, not_441_out, not_442_out,
       not_443_out, not_444_out, not_445_out, not_446_out, not_447_out, not_448_out, not_449_out,
       not_450_out, not_451_out, not_452_out, not_453_out, not_454_out, not_455_out, not_456_out,
       not_457_out, not_458_out, not_459_out, not_460_out, not_461_out, not_462_out, not_463_out,
       not_464_out, not_465_out, not_466_out, not_467_out, not_468_out, not_469_out, not_470_out,
       not_471_out, not_472_out, not_473_out, not_474_out, not_475_out, not_476_out, not_477_out,
       not_478_out, not_479_out, not_480_out, not_481_out, not_482_out, not_483_out, not_484_out,
       not_485_out, not_486_out, not_487_out, not_488_out, not_489_out, not_490_out, not_491_out,
       not_492_out, not_493_out, not_494_out, not_495_out, not_496_out, not_497_out, not_498_out,
       not_499_out, not_500_out, not_501_out, not_502_out, not_503_out, not_504_out, not_505_out,
       not_506_out, not_507_out, not_508_out, not_509_out, not_510_out, not_511_out, not_512_out,
       not_513_out, not_514_out, not_515_out, not_516_out, not_517_out, not_518_out, not_519_out,
       not_520_out, not_521_out, not_522_out, not_523_out, not_524_out, not_525_out, not_526_out,
       not_527_out, not_528_out, not_529_out, not_530_out, not_531_out, not_532_out, not_533_out,
       not_534_out, not_535_out, not_536_out, not_537_out, not_538_out, not_539_out, not_540_out,
       not_541_out, not_542_out, not_543_out, not_544_out, not_545_out, not_546_out, not_547_out,
       not_548_out, not_549_out, not_550_out, not_551_out, not_552_out, not_553_out, not_554_out,
       not_555_out, not_556_out, not_557_out, not_558_out, not_559_out, not_560_out, not_561_out,
       not_562_out, not_563_out, not_564_out, not_565_out, not_566_out, not_567_out, not_568_out,
       not_569_out, not_570_out, not_571_out, not_572_out, not_573_out, not_574_out, not_575_out,
       not_576_out, not_577_out, not_578_out, not_579_out, not_580_out, not_581_out, not_582_out,
       not_583_out, not_584_out, not_585_out, not_586_out, not_587_out, not_588_out, not_589_out,
       not_590_out, not_591_out, not_592_out, not_593_out, not_594_out, not_595_out, not_596_out,
       not_597_out, not_598_out, not_599_out, not_600_out, not_601_out, not_602_out, not_603_out,
       not_604_out, not_605_out, not_606_out, not_607_out, not_608_out, not_609_out, not_610_out,
       not_611_out, not_612_out, not_613_out, not_614_out, not_615_out, not_616_out, not_617_out,
       not_618_out, not_619_out, not_620_out, not_621_out, not_622_out, not_623_out, not_624_out,
       not_625_out, not_626_out, not_627_out, not_628_out, not_629_out, not_630_out, not_631_out,
       not_632_out, not_633_out, not_634_out, not_635_out, not_636_out, not_637_out, not_638_out,
       not_639_out, not_640_out, not_641_out, not_642_out, not_643_out, not_644_out, not_645_out,
       not_646_out, not_647_out, not_648_out, not_649_out, not_650_out, not_651_out, not_652_out,
       not_653_out, not_654_out, not_655_out, not_656_out, not_657_out, not_658_out, not_659_out,
       not_660_out, not_661_out, not_662_out, not_663_out, not_664_out, not_665_out, not_666_out,
       not_667_out, not_668_out, not_669_out, not_670_out, not_671_out, not_672_out, not_673_out,
       not_674_out, not_675_out, not_676_out, not_677_out, not_678_out, not_679_out, not_680_out,
       not_681_out, not_682_out, not_683_out, not_684_out, not_685_out, not_686_out, not_687_out,
       not_688_out, not_689_out, not_690_out, not_691_out, not_692_out, not_693_out, not_694_out,
       not_695_out, not_696_out, not_697_out, not_698_out, not_699_out, not_700_out, not_701_out,
       not_702_out, not_703_out, not_704_out, not_705_out, not_706_out, not_707_out, not_708_out,
       not_709_out, not_710_out, not_711_out, not_712_out, not_713_out, not_714_out, not_715_out,
       not_716_out, not_717_out, not_718_out, not_719_out, not_720_out, not_721_out, not_722_out,
       not_723_out, not_724_out, not_725_out, not_726_out, not_727_out, not_728_out, not_729_out,
       not_730_out, not_731_out, not_732_out, not_733_out, not_734_out, not_735_out, not_736_out,
       not_737_out, not_738_out, not_739_out, not_740_out, not_741_out, not_742_out, not_743_out,
       not_744_out, not_745_out, not_746_out, not_747_out, not_748_out, not_749_out, not_750_out,
       not_751_out, not_752_out, not_753_out, not_754_out, not_755_out, not_756_out, not_757_out,
       not_758_out, not_759_out, not_760_out, not_761_out, not_762_out, not_763_out, not_764_out,
       not_765_out, not_766_out, not_767_out, not_768_out, not_769_out, not_770_out, not_771_out,
       not_772_out, not_773_out, not_774_out, not_775_out, not_776_out, not_777_out, not_778_out,
       not_779_out, not_780_out, not_781_out, not_782_out, not_783_out, not_784_out, not_785_out,
       not_786_out, not_787_out, not_788_out, not_789_out, not_790_out, not_791_out, not_792_out,
       not_793_out, not_794_out, not_795_out, not_796_out, not_797_out, not_798_out, not_799_out,
       not_800_out, not_801_out, not_802_out, not_803_out, not_804_out, not_805_out, not_806_out,
       not_807_out, not_808_out, not_809_out, not_810_out, not_811_out, not_812_out, not_813_out,
       not_814_out, not_815_out, not_816_out, not_817_out, not_818_out, not_819_out, not_820_out,
       not_821_out, not_822_out, not_823_out, not_824_out, not_825_out, not_826_out, not_827_out,
       not_828_out, not_829_out, not_830_out, not_831_out, not_832_out, not_833_out, not_834_out,
       not_835_out, not_836_out, not_837_out, not_838_out, not_839_out, not_840_out, not_841_out,
       not_842_out, not_843_out, not_844_out, not_845_out, not_846_out, not_847_out, not_848_out,
       not_849_out, not_850_out, not_851_out, not_852_out, not_853_out, not_854_out, not_855_out,
       not_856_out, not_857_out, not_858_out, not_859_out, not_860_out, not_861_out, not_862_out,
       not_863_out, not_864_out, not_865_out, not_866_out, not_867_out, not_868_out, not_869_out,
       not_870_out, not_871_out, not_872_out, not_873_out, not_874_out, not_875_out, not_876_out,
       not_877_out, not_878_out, not_879_out, not_880_out, not_881_out, not_882_out, not_883_out,
       not_884_out, not_885_out, not_886_out, not_887_out, not_888_out, not_889_out, not_890_out,
       not_891_out, not_892_out, not_893_out, not_894_out, not_895_out, not_896_out, not_897_out,
       not_898_out, not_899_out, not_900_out, not_901_out, not_902_out, not_903_out, not_904_out,
       not_905_out, not_906_out, not_907_out, not_908_out, not_909_out, not_910_out, not_911_out,
       not_912_out, not_913_out, not_914_out, not_915_out, not_916_out, not_917_out, not_918_out,
       not_919_out, not_920_out, not_921_out, not_922_out, not_923_out, not_924_out, not_925_out,
       not_926_out, not_927_out, not_928_out, not_929_out, not_930_out, not_931_out, not_932_out,
       not_933_out, not_934_out, not_935_out, not_936_out, not_937_out, not_938_out, not_939_out,
       not_940_out, not_941_out, not_942_out, not_943_out, not_944_out, not_945_out, not_946_out,
       not_947_out, not_948_out, not_949_out, not_950_out, not_951_out, not_952_out, not_953_out,
       not_954_out, not_955_out, not_956_out, not_957_out, not_958_out, not_959_out, not_960_out,
       not_961_out, not_962_out, not_963_out, not_964_out, not_965_out, not_966_out, not_967_out,
       not_968_out, not_969_out, not_970_out, not_971_out, not_972_out, not_973_out, not_974_out,
       not_975_out, not_976_out, not_977_out, not_978_out, not_979_out, not_980_out, not_981_out,
       not_982_out, not_983_out, not_984_out, not_985_out, not_986_out, not_987_out, not_988_out,
       not_989_out, not_990_out, not_991_out, not_992_out, not_993_out, not_994_out, not_995_out,
       not_996_out, not_997_out, not_998_out, not_999_out, not_1000_out, not_1001_out, not_1002_out,
       not_1003_out, not_1004_out, not_1005_out, not_1006_out, not_1007_out, not_1008_out, not_1009_out,
       not_1010_out, not_1011_out, not_1012_out, not_1013_out, not_1014_out, not_1015_out, not_1016_out,
       not_1017_out, not_1018_out, not_1019_out, not_1020_out, not_1021_out, not_1022_out, not_1023_out,
       not_1024_out, not_1025_out, not_1026_out, not_1027_out, not_1028_out, not_1029_out, not_1030_out,
       not_1031_out, not_1032_out, not_1033_out, not_1034_out, not_1035_out, not_1036_out, not_1037_out,
       not_1038_out, not_1039_out, not_1040_out, not_1041_out, not_1042_out, not_1043_out, not_1044_out,
       not_1045_out, not_1046_out, not_1047_out, not_1048_out, not_1049_out, not_1050_out, not_1051_out,
       not_1052_out, not_1053_out, not_1054_out, not_1055_out, not_1056_out, not_1057_out, not_1058_out,
       not_1059_out, not_1060_out, not_1061_out, not_1062_out, not_1063_out, not_1064_out, not_1065_out,
       not_1066_out, not_1067_out, not_1068_out, not_1069_out, not_1070_out, not_1071_out, not_1072_out,
       not_1073_out, not_1074_out, not_1075_out, not_1076_out, not_1077_out, not_1078_out, not_1079_out,
       not_1080_out, not_1081_out, not_1082_out, not_1083_out, not_1084_out, not_1085_out, not_1086_out,
       not_1087_out, not_1088_out, not_1089_out, not_1090_out, not_1091_out, not_1092_out, not_1093_out,
       not_1094_out, not_1095_out, not_1096_out, not_1097_out, not_1098_out, not_1099_out, not_1100_out,
       not_1101_out, not_1102_out, not_1103_out, not_1104_out, not_1105_out, not_1106_out, not_1107_out,
       not_1108_out, not_1109_out, not_1110_out, not_1111_out, not_1112_out, not_1113_out, not_1114_out,
       not_1115_out, not_1116_out, not_1117_out, not_1118_out, not_1119_out, not_1120_out, not_1121_out,
       not_1122_out, not_1123_out, not_1124_out, not_1125_out, not_1126_out, not_1127_out, not_1128_out,
       not_1129_out, not_1130_out, not_1131_out, not_1132_out, or_1_out, or_2_out, or_3_out, or_4_out,
       or_5_out, or_6_out, or_8_out, or_9_out, or_10_out, or_12_out, or_13_out, or_14_out, or_15_out;

  not not_1 (not_1_out, A7);
  not not_2 (not_2_out, A6);
  not not_3 (not_3_out, A3);
  not not_4 (not_4_out, A2);
  not not_5 (not_5_out, A0);
  not not_6 (not_6_out, A6);
  not not_7 (not_7_out, A4);
  not not_8 (not_8_out, A2);
  not not_9 (not_9_out, A0);
  not not_10 (not_10_out, A7);
  not not_11 (not_11_out, A6);
  not not_12 (not_12_out, A5);
  not not_13 (not_13_out, A3);
  not not_14 (not_14_out, A7);
  not not_15 (not_15_out, A6);
  not not_16 (not_16_out, A2);
  not not_17 (not_17_out, A0);
  not not_18 (not_18_out, A7);
  not not_19 (not_19_out, A4);
  not not_20 (not_20_out, A3);
  not not_21 (not_21_out, A2);
  not not_22 (not_22_out, A6);
  not not_23 (not_23_out, A3);
  not not_24 (not_24_out, A2);
  not not_25 (not_25_out, A0);
  not not_26 (not_26_out, A7);
  not not_27 (not_27_out, A6);
  not not_28 (not_28_out, A4);
  not not_29 (not_29_out, A6);
  not not_30 (not_30_out, A4);
  not not_31 (not_31_out, A3);
  not not_32 (not_32_out, A6);
  not not_33 (not_33_out, A5);
  not not_34 (not_34_out, A4);
  not not_35 (not_35_out, A2);
  not not_36 (not_36_out, A1);
  not not_37 (not_37_out, A7);
  not not_38 (not_38_out, A5);
  not not_39 (not_39_out, A1);
  not not_40 (not_40_out, A6);
  not not_41 (not_41_out, A5);
  not not_42 (not_42_out, A2);
  not not_43 (not_43_out, A7);
  not not_44 (not_44_out, A5);
  not not_45 (not_45_out, A3);
  not not_46 (not_46_out, A6);
  not not_47 (not_47_out, A5);
  not not_48 (not_48_out, A0);
  not not_49 (not_49_out, A6);
  not not_50 (not_50_out, A1);
  not not_51 (not_51_out, A0);
  not not_52 (not_52_out, A7);
  not not_53 (not_53_out, A6);
  not not_54 (not_54_out, A4);
  not not_55 (not_55_out, A3);
  not not_56 (not_56_out, A7);
  not not_57 (not_57_out, A4);
  not not_58 (not_58_out, A3);
  not not_59 (not_59_out, A2);
  not not_60 (not_60_out, A6);
  not not_61 (not_61_out, A3);
  not not_62 (not_62_out, A2);
  not not_63 (not_63_out, A0);
  not not_64 (not_64_out, A7);
  not not_65 (not_65_out, A6);
  not not_66 (not_66_out, A4);
  not not_67 (not_67_out, A7);
  not not_68 (not_68_out, A4);
  not not_69 (not_69_out, A2);
  not not_70 (not_70_out, A6);
  not not_71 (not_71_out, A4);
  not not_72 (not_72_out, A3);
  not not_73 (not_73_out, A4);
  not not_74 (not_74_out, A3);
  not not_75 (not_75_out, A2);
  not not_76 (not_76_out, A7);
  not not_77 (not_77_out, A6);
  not not_78 (not_78_out, A3);
  not not_79 (not_79_out, A7);
  not not_80 (not_80_out, A6);
  not not_81 (not_81_out, A2);
  not not_82 (not_82_out, A1);
  not not_83 (not_83_out, A7);
  not not_84 (not_84_out, A3);
  not not_85 (not_85_out, A1);
  not not_86 (not_86_out, A7);
  not not_87 (not_87_out, A7);
  not not_88 (not_88_out, A4);
  not not_89 (not_89_out, A2);
  not not_90 (not_90_out, A4);
  not not_91 (not_91_out, A3);
  not not_92 (not_92_out, A2);
  not not_93 (not_93_out, A7);
  not not_94 (not_94_out, A4);
  not not_95 (not_95_out, A0);
  not not_96 (not_96_out, A5);
  not not_97 (not_97_out, A4);
  not not_98 (not_98_out, A1);
  not not_99 (not_99_out, A7);
  not not_100 (not_100_out, A5);
  not not_101 (not_101_out, A1);
  not not_102 (not_102_out, A7);
  not not_103 (not_103_out, A5);
  not not_104 (not_104_out, A4);
  not not_105 (not_105_out, A7);
  not not_106 (not_106_out, A4);
  not not_107 (not_107_out, A1);
  not not_108 (not_108_out, A5);
  not not_109 (not_109_out, A2);
  not not_110 (not_110_out, A0);
  not not_111 (not_111_out, A2);
  not not_112 (not_112_out, A1);
  not not_113 (not_113_out, A0);
  not not_114 (not_114_out, A7);
  not not_115 (not_115_out, A3);
  not not_116 (not_116_out, A7);
  not not_117 (not_117_out, A3);
  not not_118 (not_118_out, A2);
  not not_119 (not_119_out, A4);
  not not_120 (not_120_out, A2);
  not not_121 (not_121_out, A4);
  not not_122 (not_122_out, A0);
  not not_123 (not_123_out, A7);
  not not_124 (not_124_out, A3);
  not not_125 (not_125_out, A5);
  not not_126 (not_126_out, A4);
  not not_127 (not_127_out, A3);
  not not_128 (not_128_out, A1);
  not not_129 (not_129_out, A5);
  not not_130 (not_130_out, A4);
  not not_131 (not_131_out, A2);
  not not_132 (not_132_out, A1);
  not not_133 (not_133_out, A0);
  not not_134 (not_134_out, A6);
  not not_135 (not_135_out, A5);
  not not_136 (not_136_out, A1);
  not not_137 (not_137_out, A0);
  not not_138 (not_138_out, A5);
  not not_139 (not_139_out, A4);
  not not_140 (not_140_out, A5);
  not not_141 (not_141_out, A6);
  not not_142 (not_142_out, A2);
  not not_143 (not_143_out, A6);
  not not_144 (not_144_out, A5);
  not not_145 (not_145_out, A1);
  not not_146 (not_146_out, A6);
  not not_147 (not_147_out, A0);
  not not_148 (not_148_out, A4);
  not not_149 (not_149_out, A1);
  not not_150 (not_150_out, A1);
  not not_151 (not_151_out, A4);
  not not_152 (not_152_out, A3);
  not not_153 (not_153_out, A2);
  not not_154 (not_154_out, A0);
  not not_155 (not_155_out, A5);
  not not_156 (not_156_out, A3);
  not not_157 (not_157_out, A1);
  not not_158 (not_158_out, A5);
  not not_159 (not_159_out, A4);
  not not_160 (not_160_out, A3);
  not not_161 (not_161_out, A4);
  not not_162 (not_162_out, A3);
  not not_163 (not_163_out, A1);
  not not_164 (not_164_out, A5);
  not not_165 (not_165_out, A5);
  not not_166 (not_166_out, A1);
  not not_167 (not_167_out, A0);
  not not_168 (not_168_out, A2);
  not not_169 (not_169_out, A1);
  not not_170 (not_170_out, A7);
  not not_171 (not_171_out, A6);
  not not_172 (not_172_out, A5);
  not not_173 (not_173_out, A4);
  not not_174 (not_174_out, A2);
  not not_175 (not_175_out, A7);
  not not_176 (not_176_out, A6);
  not not_177 (not_177_out, A5);
  not not_178 (not_178_out, A3);
  not not_179 (not_179_out, A2);
  not not_180 (not_180_out, A7);
  not not_181 (not_181_out, A6);
  not not_182 (not_182_out, A5);
  not not_183 (not_183_out, A2);
  not not_184 (not_184_out, A7);
  not not_185 (not_185_out, A5);
  not not_186 (not_186_out, A3);
  not not_187 (not_187_out, A6);
  not not_188 (not_188_out, A5);
  not not_189 (not_189_out, A3);
  not not_190 (not_190_out, A2);
  not not_191 (not_191_out, A6);
  not not_192 (not_192_out, A5);
  not not_193 (not_193_out, A4);
  not not_194 (not_194_out, A1);
  not not_195 (not_195_out, A0);
  not not_196 (not_196_out, A7);
  not not_197 (not_197_out, A6);
  not not_198 (not_198_out, A5);
  not not_199 (not_199_out, A1);
  not not_200 (not_200_out, A0);
  not not_201 (not_201_out, A7);
  not not_202 (not_202_out, A5);
  not not_203 (not_203_out, A4);
  not not_204 (not_204_out, A1);
  not not_205 (not_205_out, A7);
  not not_206 (not_206_out, A5);
  not not_207 (not_207_out, A4);
  not not_208 (not_208_out, A0);
  not not_209 (not_209_out, A7);
  not not_210 (not_210_out, A6);
  not not_211 (not_211_out, A3);
  not not_212 (not_212_out, A2);
  not not_213 (not_213_out, A7);
  not not_214 (not_214_out, A6);
  not not_215 (not_215_out, A5);
  not not_216 (not_216_out, A7);
  not not_217 (not_217_out, A6);
  not not_218 (not_218_out, A1);
  not not_219 (not_219_out, A7);
  not not_220 (not_220_out, A6);
  not not_221 (not_221_out, A3);
  not not_222 (not_222_out, A2);
  not not_223 (not_223_out, A1);
  not not_224 (not_224_out, A7);
  not not_225 (not_225_out, A6);
  not not_226 (not_226_out, A2);
  not not_227 (not_227_out, A1);
  not not_228 (not_228_out, A7);
  not not_229 (not_229_out, A3);
  not not_230 (not_230_out, A1);
  not not_231 (not_231_out, A6);
  not not_232 (not_232_out, A3);
  not not_233 (not_233_out, A2);
  not not_234 (not_234_out, A1);
  not not_235 (not_235_out, A7);
  not not_236 (not_236_out, A6);
  not not_237 (not_237_out, A2);
  not not_238 (not_238_out, A0);
  not not_239 (not_239_out, A7);
  not not_240 (not_240_out, A3);
  not not_241 (not_241_out, A0);
  not not_242 (not_242_out, A6);
  not not_243 (not_243_out, A3);
  not not_244 (not_244_out, A2);
  not not_245 (not_245_out, A0);
  not not_246 (not_246_out, A7);
  not not_247 (not_247_out, A4);
  not not_248 (not_248_out, A3);
  not not_249 (not_249_out, A7);
  not not_250 (not_250_out, A4);
  not not_251 (not_251_out, A1);
  not not_252 (not_252_out, A0);
  not not_253 (not_253_out, A6);
  not not_254 (not_254_out, A4);
  not not_255 (not_255_out, A2);
  not not_256 (not_256_out, A7);
  not not_257 (not_257_out, A6);
  not not_258 (not_258_out, A5);
  not not_259 (not_259_out, A4);
  not not_260 (not_260_out, A2);
  not not_261 (not_261_out, A1);
  not not_262 (not_262_out, A0);
  not not_263 (not_263_out, A7);
  not not_264 (not_264_out, A4);
  not not_265 (not_265_out, A3);
  not not_266 (not_266_out, A7);
  not not_267 (not_267_out, A4);
  not not_268 (not_268_out, A4);
  not not_269 (not_269_out, A3);
  not not_270 (not_270_out, A4);
  not not_271 (not_271_out, A7);
  not not_272 (not_272_out, A5);
  not not_273 (not_273_out, A2);
  not not_274 (not_274_out, A7);
  not not_275 (not_275_out, A2);
  not not_276 (not_276_out, A1);
  not not_277 (not_277_out, A5);
  not not_278 (not_278_out, A1);
  not not_279 (not_279_out, A0);
  not not_280 (not_280_out, A7);
  not not_281 (not_281_out, A5);
  not not_282 (not_282_out, A1);
  not not_283 (not_283_out, A7);
  not not_284 (not_284_out, A5);
  not not_285 (not_285_out, A0);
  not not_286 (not_286_out, A7);
  not not_287 (not_287_out, A4);
  not not_288 (not_288_out, A3);
  not not_289 (not_289_out, A7);
  not not_290 (not_290_out, A3);
  not not_291 (not_291_out, A4);
  not not_292 (not_292_out, A7);
  not not_293 (not_293_out, A1);
  not not_294 (not_294_out, A0);
  not not_295 (not_295_out, A2);
  not not_296 (not_296_out, A6);
  not not_297 (not_297_out, A4);
  not not_298 (not_298_out, A3);
  not not_299 (not_299_out, A2);
  not not_300 (not_300_out, A5);
  not not_301 (not_301_out, A4);
  not not_302 (not_302_out, A3);
  not not_303 (not_303_out, A0);
  not not_304 (not_304_out, A5);
  not not_305 (not_305_out, A3);
  not not_306 (not_306_out, A1);
  not not_307 (not_307_out, A6);
  not not_308 (not_308_out, A5);
  not not_309 (not_309_out, A1);
  not not_310 (not_310_out, A6);
  not not_311 (not_311_out, A5);
  not not_312 (not_312_out, A4);
  not not_313 (not_313_out, A6);
  not not_314 (not_314_out, A5);
  not not_315 (not_315_out, A0);
  not not_316 (not_316_out, A6);
  not not_317 (not_317_out, A5);
  not not_318 (not_318_out, A2);
  not not_319 (not_319_out, A1);
  not not_320 (not_320_out, A0);
  not not_321 (not_321_out, A6);
  not not_322 (not_322_out, A3);
  not not_323 (not_323_out, A5);
  not not_324 (not_324_out, A4);
  not not_325 (not_325_out, A3);
  not not_326 (not_326_out, A1);
  not not_327 (not_327_out, A0);
  not not_328 (not_328_out, A6);
  not not_329 (not_329_out, A2);
  not not_330 (not_330_out, A3);
  not not_331 (not_331_out, A6);
  not not_332 (not_332_out, A4);
  not not_333 (not_333_out, A0);
  not not_334 (not_334_out, A6);
  not not_335 (not_335_out, A1);
  not not_336 (not_336_out, A0);
  not not_337 (not_337_out, A4);
  not not_338 (not_338_out, A1);
  not not_339 (not_339_out, A5);
  not not_340 (not_340_out, A2);
  not not_341 (not_341_out, A1);
  not not_342 (not_342_out, A5);
  not not_343 (not_343_out, A4);
  not not_344 (not_344_out, A1);
  not not_345 (not_345_out, A0);
  not not_346 (not_346_out, A4);
  not not_347 (not_347_out, A2);
  not not_348 (not_348_out, A0);
  not not_349 (not_349_out, A5);
  not not_350 (not_350_out, A2);
  not not_351 (not_351_out, A5);
  not not_352 (not_352_out, A3);
  not not_353 (not_353_out, A0);
  not not_354 (not_354_out, A3);
  not not_355 (not_355_out, A2);
  not not_356 (not_356_out, A1);
  not not_357 (not_357_out, A3);
  not not_358 (not_358_out, A1);
  not not_359 (not_359_out, A0);
  not not_360 (not_360_out, A0);
  not not_361 (not_361_out, A7);
  not not_362 (not_362_out, A5);
  not not_363 (not_363_out, A3);
  not not_364 (not_364_out, A1);
  not not_365 (not_365_out, A6);
  not not_366 (not_366_out, A5);
  not not_367 (not_367_out, A4);
  not not_368 (not_368_out, A2);
  not not_369 (not_369_out, A1);
  not not_370 (not_370_out, A7);
  not not_371 (not_371_out, A6);
  not not_372 (not_372_out, A4);
  not not_373 (not_373_out, A3);
  not not_374 (not_374_out, A7);
  not not_375 (not_375_out, A5);
  not not_376 (not_376_out, A7);
  not not_377 (not_377_out, A6);
  not not_378 (not_378_out, A2);
  not not_379 (not_379_out, A6);
  not not_380 (not_380_out, A3);
  not not_381 (not_381_out, A2);
  not not_382 (not_382_out, A6);
  not not_383 (not_383_out, A5);
  not not_384 (not_384_out, A1);
  not not_385 (not_385_out, A7);
  not not_386 (not_386_out, A6);
  not not_387 (not_387_out, A3);
  not not_388 (not_388_out, A7);
  not not_389 (not_389_out, A1);
  not not_390 (not_390_out, A7);
  not not_391 (not_391_out, A4);
  not not_392 (not_392_out, A7);
  not not_393 (not_393_out, A3);
  not not_394 (not_394_out, A7);
  not not_395 (not_395_out, A4);
  not not_396 (not_396_out, A3);
  not not_397 (not_397_out, A2);
  not not_398 (not_398_out, A5);
  not not_399 (not_399_out, A4);
  not not_400 (not_400_out, A4);
  not not_401 (not_401_out, A1);
  not not_402 (not_402_out, A5);
  not not_403 (not_403_out, A2);
  not not_404 (not_404_out, A1);
  not not_405 (not_405_out, A7);
  not not_406 (not_406_out, A3);
  not not_407 (not_407_out, A4);
  not not_408 (not_408_out, A2);
  not not_409 (not_409_out, A6);
  not not_410 (not_410_out, A5);
  not not_411 (not_411_out, A2);
  not not_412 (not_412_out, A5);
  not not_413 (not_413_out, A3);
  not not_414 (not_414_out, A5);
  not not_415 (not_415_out, A4);
  not not_416 (not_416_out, A1);
  not not_417 (not_417_out, A5);
  not not_418 (not_418_out, A1);
  not not_419 (not_419_out, A6);
  not not_420 (not_420_out, A6);
  not not_421 (not_421_out, A2);
  not not_422 (not_422_out, A1);
  not not_423 (not_423_out, A3);
  not not_424 (not_424_out, A1);
  not not_425 (not_425_out, A4);
  not not_426 (not_426_out, A3);
  not not_427 (not_427_out, A2);
  not not_428 (not_428_out, A6);
  not not_429 (not_429_out, A5);
  not not_430 (not_430_out, A4);
  not not_431 (not_431_out, A2);
  not not_432 (not_432_out, A0);
  not not_433 (not_433_out, A7);
  not not_434 (not_434_out, A6);
  not not_435 (not_435_out, A5);
  not not_436 (not_436_out, A3);
  not not_437 (not_437_out, A2);
  not not_438 (not_438_out, A7);
  not not_439 (not_439_out, A6);
  not not_440 (not_440_out, A5);
  not not_441 (not_441_out, A2);
  not not_442 (not_442_out, A0);
  not not_443 (not_443_out, A7);
  not not_444 (not_444_out, A5);
  not not_445 (not_445_out, A3);
  not not_446 (not_446_out, A0);
  not not_447 (not_447_out, A6);
  not not_448 (not_448_out, A5);
  not not_449 (not_449_out, A3);
  not not_450 (not_450_out, A2);
  not not_451 (not_451_out, A0);
  not not_452 (not_452_out, A7);
  not not_453 (not_453_out, A6);
  not not_454 (not_454_out, A5);
  not not_455 (not_455_out, A4);
  not not_456 (not_456_out, A1);
  not not_457 (not_457_out, A7);
  not not_458 (not_458_out, A6);
  not not_459 (not_459_out, A5);
  not not_460 (not_460_out, A4);
  not not_461 (not_461_out, A1);
  not not_462 (not_462_out, A7);
  not not_463 (not_463_out, A6);
  not not_464 (not_464_out, A5);
  not not_465 (not_465_out, A4);
  not not_466 (not_466_out, A7);
  not not_467 (not_467_out, A6);
  not not_468 (not_468_out, A4);
  not not_469 (not_469_out, A1);
  not not_470 (not_470_out, A7);
  not not_471 (not_471_out, A6);
  not not_472 (not_472_out, A3);
  not not_473 (not_473_out, A2);
  not not_474 (not_474_out, A0);
  not not_475 (not_475_out, A7);
  not not_476 (not_476_out, A6);
  not not_477 (not_477_out, A5);
  not not_478 (not_478_out, A3);
  not not_479 (not_479_out, A7);
  not not_480 (not_480_out, A5);
  not not_481 (not_481_out, A3);
  not not_482 (not_482_out, A2);
  not not_483 (not_483_out, A6);
  not not_484 (not_484_out, A5);
  not not_485 (not_485_out, A0);
  not not_486 (not_486_out, A6);
  not not_487 (not_487_out, A1);
  not not_488 (not_488_out, A0);
  not not_489 (not_489_out, A6);
  not not_490 (not_490_out, A5);
  not not_491 (not_491_out, A2);
  not not_492 (not_492_out, A1);
  not not_493 (not_493_out, A7);
  not not_494 (not_494_out, A5);
  not not_495 (not_495_out, A1);
  not not_496 (not_496_out, A7);
  not not_497 (not_497_out, A6);
  not not_498 (not_498_out, A3);
  not not_499 (not_499_out, A2);
  not not_500 (not_500_out, A1);
  not not_501 (not_501_out, A7);
  not not_502 (not_502_out, A6);
  not not_503 (not_503_out, A2);
  not not_504 (not_504_out, A1);
  not not_505 (not_505_out, A0);
  not not_506 (not_506_out, A7);
  not not_507 (not_507_out, A3);
  not not_508 (not_508_out, A1);
  not not_509 (not_509_out, A0);
  not not_510 (not_510_out, A6);
  not not_511 (not_511_out, A3);
  not not_512 (not_512_out, A2);
  not not_513 (not_513_out, A1);
  not not_514 (not_514_out, A0);
  not not_515 (not_515_out, A7);
  not not_516 (not_516_out, A4);
  not not_517 (not_517_out, A3);
  not not_518 (not_518_out, A7);
  not not_519 (not_519_out, A4);
  not not_520 (not_520_out, A3);
  not not_521 (not_521_out, A0);
  not not_522 (not_522_out, A7);
  not not_523 (not_523_out, A6);
  not not_524 (not_524_out, A2);
  not not_525 (not_525_out, A7);
  not not_526 (not_526_out, A0);
  not not_527 (not_527_out, A7);
  not not_528 (not_528_out, A6);
  not not_529 (not_529_out, A3);
  not not_530 (not_530_out, A7);
  not not_531 (not_531_out, A6);
  not not_532 (not_532_out, A7);
  not not_533 (not_533_out, A2);
  not not_534 (not_534_out, A7);
  not not_535 (not_535_out, A5);
  not not_536 (not_536_out, A4);
  not not_537 (not_537_out, A3);
  not not_538 (not_538_out, A1);
  not not_539 (not_539_out, A7);
  not not_540 (not_540_out, A4);
  not not_541 (not_541_out, A0);
  not not_542 (not_542_out, A4);
  not not_543 (not_543_out, A3);
  not not_544 (not_544_out, A0);
  not not_545 (not_545_out, A7);
  not not_546 (not_546_out, A5);
  not not_547 (not_547_out, A3);
  not not_548 (not_548_out, A1);
  not not_549 (not_549_out, A7);
  not not_550 (not_550_out, A5);
  not not_551 (not_551_out, A2);
  not not_552 (not_552_out, A1);
  not not_553 (not_553_out, A7);
  not not_554 (not_554_out, A5);
  not not_555 (not_555_out, A4);
  not not_556 (not_556_out, A5);
  not not_557 (not_557_out, A2);
  not not_558 (not_558_out, A0);
  not not_559 (not_559_out, A2);
  not not_560 (not_560_out, A1);
  not not_561 (not_561_out, A0);
  not not_562 (not_562_out, A7);
  not not_563 (not_563_out, A5);
  not not_564 (not_564_out, A7);
  not not_565 (not_565_out, A4);
  not not_566 (not_566_out, A3);
  not not_567 (not_567_out, A0);
  not not_568 (not_568_out, A7);
  not not_569 (not_569_out, A3);
  not not_570 (not_570_out, A7);
  not not_571 (not_571_out, A4);
  not not_572 (not_572_out, A1);
  not not_573 (not_573_out, A7);
  not not_574 (not_574_out, A1);
  not not_575 (not_575_out, A7);
  not not_576 (not_576_out, A3);
  not not_577 (not_577_out, A2);
  not not_578 (not_578_out, A6);
  not not_579 (not_579_out, A5);
  not not_580 (not_580_out, A4);
  not not_581 (not_581_out, A1);
  not not_582 (not_582_out, A0);
  not not_583 (not_583_out, A6);
  not not_584 (not_584_out, A4);
  not not_585 (not_585_out, A2);
  not not_586 (not_586_out, A0);
  not not_587 (not_587_out, A6);
  not not_588 (not_588_out, A5);
  not not_589 (not_589_out, A3);
  not not_590 (not_590_out, A1);
  not not_591 (not_591_out, A6);
  not not_592 (not_592_out, A5);
  not not_593 (not_593_out, A4);
  not not_594 (not_594_out, A3);
  not not_595 (not_595_out, A6);
  not not_596 (not_596_out, A4);
  not not_597 (not_597_out, A3);
  not not_598 (not_598_out, A1);
  not not_599 (not_599_out, A5);
  not not_600 (not_600_out, A2);
  not not_601 (not_601_out, A1);
  not not_602 (not_602_out, A0);
  not not_603 (not_603_out, A5);
  not not_604 (not_604_out, A4);
  not not_605 (not_605_out, A2);
  not not_606 (not_606_out, A5);
  not not_607 (not_607_out, A4);
  not not_608 (not_608_out, A0);
  not not_609 (not_609_out, A6);
  not not_610 (not_610_out, A5);
  not not_611 (not_611_out, A6);
  not not_612 (not_612_out, A0);
  not not_613 (not_613_out, A6);
  not not_614 (not_614_out, A3);
  not not_615 (not_615_out, A2);
  not not_616 (not_616_out, A6);
  not not_617 (not_617_out, A2);
  not not_618 (not_618_out, A0);
  not not_619 (not_619_out, A3);
  not not_620 (not_620_out, A0);
  not not_621 (not_621_out, A4);
  not not_622 (not_622_out, A1);
  not not_623 (not_623_out, A0);
  not not_624 (not_624_out, A6);
  not not_625 (not_625_out, A1);
  not not_626 (not_626_out, A6);
  not not_627 (not_627_out, A4);
  not not_628 (not_628_out, A6);
  not not_629 (not_629_out, A3);
  not not_630 (not_630_out, A3);
  not not_631 (not_631_out, A2);
  not not_632 (not_632_out, A5);
  not not_633 (not_633_out, A3);
  not not_634 (not_634_out, A2);
  not not_635 (not_635_out, A1);
  not not_636 (not_636_out, A5);
  not not_637 (not_637_out, A4);
  not not_638 (not_638_out, A3);
  not not_639 (not_639_out, A5);
  not not_640 (not_640_out, A4);
  not not_641 (not_641_out, A1);
  not not_642 (not_642_out, A5);
  not not_643 (not_643_out, A3);
  not not_644 (not_644_out, A1);
  not not_645 (not_645_out, A5);
  not not_646 (not_646_out, A1);
  not not_647 (not_647_out, A0);
  not not_648 (not_648_out, A2);
  not not_649 (not_649_out, A0);
  not not_650 (not_650_out, A5);
  not not_651 (not_651_out, A3);
  not not_652 (not_652_out, A5);
  not not_653 (not_653_out, A4);
  not not_654 (not_654_out, A3);
  not not_655 (not_655_out, A1);
  not not_656 (not_656_out, A3);
  not not_657 (not_657_out, A1);
  not not_658 (not_658_out, A4);
  not not_659 (not_659_out, A2);
  not not_660 (not_660_out, A4);
  not not_661 (not_661_out, A1);
  not not_662 (not_662_out, A6);
  not not_663 (not_663_out, A5);
  not not_664 (not_664_out, A4);
  not not_665 (not_665_out, A2);
  not not_666 (not_666_out, A0);
  not not_667 (not_667_out, A7);
  not not_668 (not_668_out, A6);
  not not_669 (not_669_out, A5);
  not not_670 (not_670_out, A2);
  not not_671 (not_671_out, A0);
  not not_672 (not_672_out, A7);
  not not_673 (not_673_out, A5);
  not not_674 (not_674_out, A3);
  not not_675 (not_675_out, A0);
  not not_676 (not_676_out, A6);
  not not_677 (not_677_out, A5);
  not not_678 (not_678_out, A3);
  not not_679 (not_679_out, A2);
  not not_680 (not_680_out, A0);
  not not_681 (not_681_out, A7);
  not not_682 (not_682_out, A5);
  not not_683 (not_683_out, A4);
  not not_684 (not_684_out, A1);
  not not_685 (not_685_out, A0);
  not not_686 (not_686_out, A7);
  not not_687 (not_687_out, A6);
  not not_688 (not_688_out, A3);
  not not_689 (not_689_out, A2);
  not not_690 (not_690_out, A0);
  not not_691 (not_691_out, A6);
  not not_692 (not_692_out, A5);
  not not_693 (not_693_out, A0);
  not not_694 (not_694_out, A6);
  not not_695 (not_695_out, A1);
  not not_696 (not_696_out, A0);
  not not_697 (not_697_out, A7);
  not not_698 (not_698_out, A6);
  not not_699 (not_699_out, A2);
  not not_700 (not_700_out, A1);
  not not_701 (not_701_out, A0);
  not not_702 (not_702_out, A7);
  not not_703 (not_703_out, A3);
  not not_704 (not_704_out, A1);
  not not_705 (not_705_out, A0);
  not not_706 (not_706_out, A6);
  not not_707 (not_707_out, A3);
  not not_708 (not_708_out, A2);
  not not_709 (not_709_out, A1);
  not not_710 (not_710_out, A0);
  not not_711 (not_711_out, A7);
  not not_712 (not_712_out, A4);
  not not_713 (not_713_out, A3);
  not not_714 (not_714_out, A0);
  not not_715 (not_715_out, A7);
  not not_716 (not_716_out, A0);
  not not_717 (not_717_out, A7);
  not not_718 (not_718_out, A4);
  not not_719 (not_719_out, A0);
  not not_720 (not_720_out, A4);
  not not_721 (not_721_out, A3);
  not not_722 (not_722_out, A0);
  not not_723 (not_723_out, A7);
  not not_724 (not_724_out, A5);
  not not_725 (not_725_out, A1);
  not not_726 (not_726_out, A0);
  not not_727 (not_727_out, A5);
  not not_728 (not_728_out, A2);
  not not_729 (not_729_out, A0);
  not not_730 (not_730_out, A2);
  not not_731 (not_731_out, A1);
  not not_732 (not_732_out, A0);
  not not_733 (not_733_out, A7);
  not not_734 (not_734_out, A4);
  not not_735 (not_735_out, A3);
  not not_736 (not_736_out, A0);
  not not_737 (not_737_out, A7);
  not not_738 (not_738_out, A3);
  not not_739 (not_739_out, A0);
  not not_740 (not_740_out, A4);
  not not_741 (not_741_out, A0);
  not not_742 (not_742_out, A6);
  not not_743 (not_743_out, A5);
  not not_744 (not_744_out, A4);
  not not_745 (not_745_out, A1);
  not not_746 (not_746_out, A0);
  not not_747 (not_747_out, A6);
  not not_748 (not_748_out, A4);
  not not_749 (not_749_out, A2);
  not not_750 (not_750_out, A0);
  not not_751 (not_751_out, A5);
  not not_752 (not_752_out, A4);
  not not_753 (not_753_out, A2);
  not not_754 (not_754_out, A1);
  not not_755 (not_755_out, A0);
  not not_756 (not_756_out, A6);
  not not_757 (not_757_out, A5);
  not not_758 (not_758_out, A1);
  not not_759 (not_759_out, A0);
  not not_760 (not_760_out, A5);
  not not_761 (not_761_out, A4);
  not not_762 (not_762_out, A0);
  not not_763 (not_763_out, A6);
  not not_764 (not_764_out, A0);
  not not_765 (not_765_out, A6);
  not not_766 (not_766_out, A2);
  not not_767 (not_767_out, A0);
  not not_768 (not_768_out, A3);
  not not_769 (not_769_out, A0);
  not not_770 (not_770_out, A4);
  not not_771 (not_771_out, A1);
  not not_772 (not_772_out, A0);
  not not_773 (not_773_out, A5);
  not not_774 (not_774_out, A1);
  not not_775 (not_775_out, A0);
  not not_776 (not_776_out, A2);
  not not_777 (not_777_out, A0);
  not not_778 (not_778_out, A5);
  not not_779 (not_779_out, A0);
  not not_780 (not_780_out, A1);
  not not_781 (not_781_out, A0);
  not not_782 (not_782_out, A7);
  not not_783 (not_783_out, A5);
  not not_784 (not_784_out, A3);
  not not_785 (not_785_out, A1);
  not not_786 (not_786_out, A0);
  not not_787 (not_787_out, A7);
  not not_788 (not_788_out, A6);
  not not_789 (not_789_out, A4);
  not not_790 (not_790_out, A3);
  not not_791 (not_791_out, A0);
  not not_792 (not_792_out, A7);
  not not_793 (not_793_out, A5);
  not not_794 (not_794_out, A4);
  not not_795 (not_795_out, A3);
  not not_796 (not_796_out, A1);
  not not_797 (not_797_out, A7);
  not not_798 (not_798_out, A6);
  not not_799 (not_799_out, A5);
  not not_800 (not_800_out, A2);
  not not_801 (not_801_out, A1);
  not not_802 (not_802_out, A7);
  not not_803 (not_803_out, A5);
  not not_804 (not_804_out, A0);
  not not_805 (not_805_out, A7);
  not not_806 (not_806_out, A5);
  not not_807 (not_807_out, A4);
  not not_808 (not_808_out, A7);
  not not_809 (not_809_out, A6);
  not not_810 (not_810_out, A2);
  not not_811 (not_811_out, A0);
  not not_812 (not_812_out, A7);
  not not_813 (not_813_out, A6);
  not not_814 (not_814_out, A5);
  not not_815 (not_815_out, A3);
  not not_816 (not_816_out, A2);
  not not_817 (not_817_out, A6);
  not not_818 (not_818_out, A5);
  not not_819 (not_819_out, A1);
  not not_820 (not_820_out, A0);
  not not_821 (not_821_out, A7);
  not not_822 (not_822_out, A6);
  not not_823 (not_823_out, A5);
  not not_824 (not_824_out, A1);
  not not_825 (not_825_out, A7);
  not not_826 (not_826_out, A5);
  not not_827 (not_827_out, A2);
  not not_828 (not_828_out, A1);
  not not_829 (not_829_out, A7);
  not not_830 (not_830_out, A6);
  not not_831 (not_831_out, A4);
  not not_832 (not_832_out, A3);
  not not_833 (not_833_out, A6);
  not not_834 (not_834_out, A4);
  not not_835 (not_835_out, A0);
  not not_836 (not_836_out, A7);
  not not_837 (not_837_out, A1);
  not not_838 (not_838_out, A0);
  not not_839 (not_839_out, A7);
  not not_840 (not_840_out, A4);
  not not_841 (not_841_out, A1);
  not not_842 (not_842_out, A7);
  not not_843 (not_843_out, A6);
  not not_844 (not_844_out, A3);
  not not_845 (not_845_out, A2);
  not not_846 (not_846_out, A1);
  not not_847 (not_847_out, A7);
  not not_848 (not_848_out, A3);
  not not_849 (not_849_out, A7);
  not not_850 (not_850_out, A6);
  not not_851 (not_851_out, A2);
  not not_852 (not_852_out, A7);
  not not_853 (not_853_out, A5);
  not not_854 (not_854_out, A4);
  not not_855 (not_855_out, A3);
  not not_856 (not_856_out, A1);
  not not_857 (not_857_out, A7);
  not not_858 (not_858_out, A4);
  not not_859 (not_859_out, A3);
  not not_860 (not_860_out, A2);
  not not_861 (not_861_out, A0);
  not not_862 (not_862_out, A7);
  not not_863 (not_863_out, A5);
  not not_864 (not_864_out, A3);
  not not_865 (not_865_out, A1);
  not not_866 (not_866_out, A5);
  not not_867 (not_867_out, A4);
  not not_868 (not_868_out, A0);
  not not_869 (not_869_out, A4);
  not not_870 (not_870_out, A1);
  not not_871 (not_871_out, A0);
  not not_872 (not_872_out, A7);
  not not_873 (not_873_out, A5);
  not not_874 (not_874_out, A4);
  not not_875 (not_875_out, A7);
  not not_876 (not_876_out, A5);
  not not_877 (not_877_out, A7);
  not not_878 (not_878_out, A3);
  not not_879 (not_879_out, A0);
  not not_880 (not_880_out, A7);
  not not_881 (not_881_out, A3);
  not not_882 (not_882_out, A2);
  not not_883 (not_883_out, A7);
  not not_884 (not_884_out, A4);
  not not_885 (not_885_out, A1);
  not not_886 (not_886_out, A7);
  not not_887 (not_887_out, A4);
  not not_888 (not_888_out, A0);
  not not_889 (not_889_out, A7);
  not not_890 (not_890_out, A1);
  not not_891 (not_891_out, A0);
  not not_892 (not_892_out, A6);
  not not_893 (not_893_out, A5);
  not not_894 (not_894_out, A3);
  not not_895 (not_895_out, A2);
  not not_896 (not_896_out, A1);
  not not_897 (not_897_out, A5);
  not not_898 (not_898_out, A3);
  not not_899 (not_899_out, A0);
  not not_900 (not_900_out, A5);
  not not_901 (not_901_out, A4);
  not not_902 (not_902_out, A3);
  not not_903 (not_903_out, A5);
  not not_904 (not_904_out, A4);
  not not_905 (not_905_out, A1);
  not not_906 (not_906_out, A0);
  not not_907 (not_907_out, A6);
  not not_908 (not_908_out, A5);
  not not_909 (not_909_out, A2);
  not not_910 (not_910_out, A6);
  not not_911 (not_911_out, A5);
  not not_912 (not_912_out, A3);
  not not_913 (not_913_out, A1);
  not not_914 (not_914_out, A5);
  not not_915 (not_915_out, A3);
  not not_916 (not_916_out, A2);
  not not_917 (not_917_out, A1);
  not not_918 (not_918_out, A6);
  not not_919 (not_919_out, A5);
  not not_920 (not_920_out, A5);
  not not_921 (not_921_out, A2);
  not not_922 (not_922_out, A3);
  not not_923 (not_923_out, A1);
  not not_924 (not_924_out, A0);
  not not_925 (not_925_out, A4);
  not not_926 (not_926_out, A3);
  not not_927 (not_927_out, A1);
  not not_928 (not_928_out, A6);
  not not_929 (not_929_out, A2);
  not not_930 (not_930_out, A1);
  not not_931 (not_931_out, A0);
  not not_932 (not_932_out, A4);
  not not_933 (not_933_out, A6);
  not not_934 (not_934_out, A3);
  not not_935 (not_935_out, A2);
  not not_936 (not_936_out, A6);
  not not_937 (not_937_out, A1);
  not not_938 (not_938_out, A2);
  not not_939 (not_939_out, A1);
  not not_940 (not_940_out, A5);
  not not_941 (not_941_out, A4);
  not not_942 (not_942_out, A3);
  not not_943 (not_943_out, A5);
  not not_944 (not_944_out, A3);
  not not_945 (not_945_out, A5);
  not not_946 (not_946_out, A1);
  not not_947 (not_947_out, A0);
  not not_948 (not_948_out, A5);
  not not_949 (not_949_out, A4);
  not not_950 (not_950_out, A1);
  not not_951 (not_951_out, A4);
  not not_952 (not_952_out, A3);
  not not_953 (not_953_out, A1);
  not not_954 (not_954_out, A4);
  not not_955 (not_955_out, A3);
  not not_956 (not_956_out, A0);
  not not_957 (not_957_out, A3);
  not not_958 (not_958_out, A1);
  not not_959 (not_959_out, A4);
  not not_960 (not_960_out, A7);
  not not_961 (not_961_out, A6);
  not not_962 (not_962_out, A5);
  not not_963 (not_963_out, A3);
  not not_964 (not_964_out, A2);
  not not_965 (not_965_out, A7);
  not not_966 (not_966_out, A6);
  not not_967 (not_967_out, A5);
  not not_968 (not_968_out, A4);
  not not_969 (not_969_out, A1);
  not not_970 (not_970_out, A7);
  not not_971 (not_971_out, A6);
  not not_972 (not_972_out, A4);
  not not_973 (not_973_out, A0);
  not not_974 (not_974_out, A6);
  not not_975 (not_975_out, A4);
  not not_976 (not_976_out, A3);
  not not_977 (not_977_out, A0);
  not not_978 (not_978_out, A7);
  not not_979 (not_979_out, A6);
  not not_980 (not_980_out, A5);
  not not_981 (not_981_out, A1);
  not not_982 (not_982_out, A7);
  not not_983 (not_983_out, A5);
  not not_984 (not_984_out, A2);
  not not_985 (not_985_out, A1);
  not not_986 (not_986_out, A7);
  not not_987 (not_987_out, A6);
  not not_988 (not_988_out, A5);
  not not_989 (not_989_out, A4);
  not not_990 (not_990_out, A7);
  not not_991 (not_991_out, A6);
  not not_992 (not_992_out, A4);
  not not_993 (not_993_out, A1);
  not not_994 (not_994_out, A6);
  not not_995 (not_995_out, A5);
  not not_996 (not_996_out, A2);
  not not_997 (not_997_out, A0);
  not not_998 (not_998_out, A6);
  not not_999 (not_999_out, A2);
  not not_1000 (not_1000_out, A1);
  not not_1001 (not_1001_out, A0);
  not not_1002 (not_1002_out, A7);
  not not_1003 (not_1003_out, A6);
  not not_1004 (not_1004_out, A5);
  not not_1005 (not_1005_out, A3);
  not not_1006 (not_1006_out, A7);
  not not_1007 (not_1007_out, A5);
  not not_1008 (not_1008_out, A3);
  not not_1009 (not_1009_out, A2);
  not not_1010 (not_1010_out, A7);
  not not_1011 (not_1011_out, A6);
  not not_1012 (not_1012_out, A3);
  not not_1013 (not_1013_out, A2);
  not not_1014 (not_1014_out, A1);
  not not_1015 (not_1015_out, A7);
  not not_1016 (not_1016_out, A4);
  not not_1017 (not_1017_out, A3);
  not not_1018 (not_1018_out, A7);
  not not_1019 (not_1019_out, A6);
  not not_1020 (not_1020_out, A2);
  not not_1021 (not_1021_out, A7);
  not not_1022 (not_1022_out, A6);
  not not_1023 (not_1023_out, A3);
  not not_1024 (not_1024_out, A7);
  not not_1025 (not_1025_out, A6);
  not not_1026 (not_1026_out, A7);
  not not_1027 (not_1027_out, A5);
  not not_1028 (not_1028_out, A4);
  not not_1029 (not_1029_out, A3);
  not not_1030 (not_1030_out, A1);
  not not_1031 (not_1031_out, A7);
  not not_1032 (not_1032_out, A4);
  not not_1033 (not_1033_out, A2);
  not not_1034 (not_1034_out, A0);
  not not_1035 (not_1035_out, A5);
  not not_1036 (not_1036_out, A4);
  not not_1037 (not_1037_out, A1);
  not not_1038 (not_1038_out, A0);
  not not_1039 (not_1039_out, A7);
  not not_1040 (not_1040_out, A5);
  not not_1041 (not_1041_out, A4);
  not not_1042 (not_1042_out, A7);
  not not_1043 (not_1043_out, A5);
  not not_1044 (not_1044_out, A1);
  not not_1045 (not_1045_out, A7);
  not not_1046 (not_1046_out, A0);
  not not_1047 (not_1047_out, A3);
  not not_1048 (not_1048_out, A0);
  not not_1049 (not_1049_out, A7);
  not not_1050 (not_1050_out, A5);
  not not_1051 (not_1051_out, A4);
  not not_1052 (not_1052_out, A2);
  not not_1053 (not_1053_out, A0);
  not not_1054 (not_1054_out, A7);
  not not_1055 (not_1055_out, A3);
  not not_1056 (not_1056_out, A7);
  not not_1057 (not_1057_out, A4);
  not not_1058 (not_1058_out, A1);
  not not_1059 (not_1059_out, A7);
  not not_1060 (not_1060_out, A1);
  not not_1061 (not_1061_out, A7);
  not not_1062 (not_1062_out, A3);
  not not_1063 (not_1063_out, A2);
  not not_1064 (not_1064_out, A7);
  not not_1065 (not_1065_out, A2);
  not not_1066 (not_1066_out, A6);
  not not_1067 (not_1067_out, A5);
  not not_1068 (not_1068_out, A3);
  not not_1069 (not_1069_out, A1);
  not not_1070 (not_1070_out, A6);
  not not_1071 (not_1071_out, A5);
  not not_1072 (not_1072_out, A2);
  not not_1073 (not_1073_out, A1);
  not not_1074 (not_1074_out, A0);
  not not_1075 (not_1075_out, A5);
  not not_1076 (not_1076_out, A3);
  not not_1077 (not_1077_out, A2);
  not not_1078 (not_1078_out, A1);
  not not_1079 (not_1079_out, A6);
  not not_1080 (not_1080_out, A5);
  not not_1081 (not_1081_out, A4);
  not not_1082 (not_1082_out, A3);
  not not_1083 (not_1083_out, A6);
  not not_1084 (not_1084_out, A5);
  not not_1085 (not_1085_out, A5);
  not not_1086 (not_1086_out, A2);
  not not_1087 (not_1087_out, A6);
  not not_1088 (not_1088_out, A5);
  not not_1089 (not_1089_out, A2);
  not not_1090 (not_1090_out, A1);
  not not_1091 (not_1091_out, A6);
  not not_1092 (not_1092_out, A5);
  not not_1093 (not_1093_out, A1);
  not not_1094 (not_1094_out, A0);
  not not_1095 (not_1095_out, A6);
  not not_1096 (not_1096_out, A2);
  not not_1097 (not_1097_out, A0);
  not not_1098 (not_1098_out, A5);
  not not_1099 (not_1099_out, A2);
  not not_1100 (not_1100_out, A1);
  not not_1101 (not_1101_out, A0);
  not not_1102 (not_1102_out, A6);
  not not_1103 (not_1103_out, A3);
  not not_1104 (not_1104_out, A2);
  not not_1105 (not_1105_out, A4);
  not not_1106 (not_1106_out, A3);
  not not_1107 (not_1107_out, A1);
  not not_1108 (not_1108_out, A6);
  not not_1109 (not_1109_out, A1);
  not not_1110 (not_1110_out, A4);
  not not_1111 (not_1111_out, A6);
  not not_1112 (not_1112_out, A3);
  not not_1113 (not_1113_out, A3);
  not not_1114 (not_1114_out, A2);
  not not_1115 (not_1115_out, A1);
  not not_1116 (not_1116_out, A5);
  not not_1117 (not_1117_out, A4);
  not not_1118 (not_1118_out, A3);
  not not_1119 (not_1119_out, A5);
  not not_1120 (not_1120_out, A4);
  not not_1121 (not_1121_out, A1);
  not not_1122 (not_1122_out, A4);
  not not_1123 (not_1123_out, A0);
  not not_1124 (not_1124_out, A5);
  not not_1125 (not_1125_out, A3);
  not not_1126 (not_1126_out, A4);
  not not_1127 (not_1127_out, A2);
  not not_1128 (not_1128_out, A1);
  not not_1129 (not_1129_out, A3);
  not not_1130 (not_1130_out, A1);
  not not_1131 (not_1131_out, A4);
  not not_1132 (not_1132_out, A2);
  and and_1 (and_1_out, not_1_out, not_2_out, not_3_out, not_4_out, not_5_out);
  and and_2 (and_2_out, not_6_out, not_7_out, not_8_out, not_9_out);
  and and_3 (and_3_out, not_10_out, not_11_out, not_12_out, not_13_out, A1);
  and and_4 (and_4_out, not_14_out, not_15_out, not_16_out, A1, not_17_out);
  and and_5 (and_5_out, not_18_out, not_19_out, not_20_out, not_21_out, A1);
  and and_6 (and_6_out, not_22_out, not_23_out, not_24_out, A1, not_25_out);
  and and_7 (and_7_out, not_26_out, not_27_out, not_28_out, A2, A0);
  and and_8 (and_8_out, not_29_out, not_30_out, not_31_out, A2, A0);
  and and_9 (and_9_out, not_32_out, not_33_out, not_34_out, A3, not_35_out, not_36_out);
  and and_10 (and_10_out, not_37_out, not_38_out, A3, A2, not_39_out);
  and and_11 (and_11_out, not_40_out, not_41_out, A4, not_42_out, A0);
  and and_12 (and_12_out, not_43_out, not_44_out, A4, not_45_out, A1);
  and and_13 (and_13_out, not_46_out, not_47_out, A4, A2, not_48_out);
  and and_14 (and_14_out, not_49_out, A4, A2, not_50_out, not_51_out);
  and and_15 (and_15_out, not_52_out, not_53_out, A5, not_54_out, not_55_out);
  and and_16 (and_16_out, not_56_out, A5, not_57_out, not_58_out, not_59_out);
  and and_17 (and_17_out, not_60_out, A5, not_61_out, not_62_out, not_63_out);
  and and_18 (and_18_out, not_64_out, not_65_out, A5, not_66_out, A1);
  and and_19 (and_19_out, not_67_out, A5, not_68_out, not_69_out, A1);
  and and_20 (and_20_out, not_70_out, A5, not_71_out, not_72_out, A1);
  and and_21 (and_21_out, A5, not_73_out, not_74_out, not_75_out, A1);
  and and_22 (and_22_out, not_76_out, not_77_out, A5, not_78_out, A2, A0);
  and and_23 (and_23_out, not_79_out, not_80_out, A5, A4, not_81_out, not_82_out);
  and and_24 (and_24_out, not_83_out, A5, A4, not_84_out, not_85_out);
  and and_25 (and_25_out, not_86_out, A5, A4, A3, A1);
  and and_26 (and_26_out, not_87_out, A6, not_88_out, not_89_out, A0);
  and and_27 (and_27_out, A6, not_90_out, not_91_out, not_92_out, A0);
  and and_28 (and_28_out, not_93_out, A6, not_94_out, A2, not_95_out);
  and and_29 (and_29_out, A6, not_96_out, not_97_out, A2, not_98_out, A0);
  and and_30 (and_30_out, not_99_out, A6, not_100_out, A3, not_101_out);
  and and_31 (and_31_out, not_102_out, A6, not_103_out, not_104_out, A3, A2);
  and and_32 (and_32_out, not_105_out, A6, not_106_out, A3, A2, not_107_out);
  and and_33 (and_33_out, A6, not_108_out, A4, not_109_out, not_110_out);
  and and_34 (and_34_out, A6, A4, not_111_out, not_112_out, not_113_out);
  and and_35 (and_35_out, not_114_out, A6, A4, A2, A0);
  and and_36 (and_36_out, A6, A4, not_115_out, A2, A0);
  and and_37 (and_37_out, not_116_out, A6, A5, not_117_out, not_118_out, A0);
  and and_38 (and_38_out, A6, A5, not_119_out, not_120_out, A0);
  and and_39 (and_39_out, A6, A5, not_121_out, A2, not_122_out);
  and and_40 (and_40_out, not_123_out, A6, A5, not_124_out, A2, A1);
  and and_41 (and_41_out, A6, A5, A4, A2, A0);
  and and_42 (and_42_out, A7, not_125_out, not_126_out, not_127_out, not_128_out);
  and and_43 (and_43_out, A7, not_129_out, not_130_out, not_131_out, not_132_out, not_133_out);
  and and_44 (and_44_out, A7, not_134_out, not_135_out, A3, not_136_out, not_137_out);
  and and_45 (and_45_out, A7, not_138_out, not_139_out, A3, A1);
  and and_46 (and_46_out, A7, not_140_out, A3, A2, A1);
  and and_47 (and_47_out, A7, not_141_out, A4, not_142_out, A0);
  and and_48 (and_48_out, A7, not_143_out, not_144_out, A4, A2, not_145_out);
  and and_49 (and_49_out, A7, not_146_out, A4, A2, not_147_out);
  and and_50 (and_50_out, A7, A5, not_148_out, A3, not_149_out);
  and and_51 (and_51_out, A7, A5, A3, A2, not_150_out);
  and and_52 (and_52_out, A7, A5, not_151_out, A3, A2, A0);
  and and_53 (and_53_out, A7, A5, A4, not_152_out, A1);
  and and_54 (and_54_out, A7, A5, A4, not_153_out, A1, not_154_out);
  and and_55 (and_55_out, A7, A6, not_155_out, not_156_out, not_157_out);
  and and_56 (and_56_out, A7, A6, not_158_out, not_159_out, not_160_out, A2);
  and and_57 (and_57_out, A7, A6, not_161_out, not_162_out, A2, not_163_out);
  and and_58 (and_58_out, A7, A6, not_164_out, A3, A1);
  and and_59 (and_59_out, A7, A6, not_165_out, A4, not_166_out, not_167_out);
  and and_60 (and_60_out, A7, A6, A4, A3, not_168_out, not_169_out);
  and and_61 (and_61_out, not_170_out, not_171_out, not_172_out, not_173_out, not_174_out);
  and and_62 (and_62_out, not_175_out, not_176_out, not_177_out, not_178_out, not_179_out, A0);
  and and_63 (and_63_out, not_180_out, not_181_out, not_182_out, not_183_out, A1, A0);
  and and_64 (and_64_out, not_184_out, not_185_out, not_186_out, A1, A0);
  and and_65 (and_65_out, not_187_out, not_188_out, not_189_out, not_190_out, A1, A0);
  and and_66 (and_66_out, not_191_out, not_192_out, not_193_out, A2, not_194_out, not_195_out);
  and and_67 (and_67_out, not_196_out, not_197_out, not_198_out, A3, not_199_out, not_200_out);
  and and_68 (and_68_out, not_201_out, not_202_out, not_203_out, A3, not_204_out, A0);
  and and_69 (and_69_out, not_205_out, not_206_out, not_207_out, A3, A1, not_208_out);
  and and_70 (and_70_out, not_209_out, not_210_out, A4, not_211_out, not_212_out, A1);
  and and_71 (and_71_out, not_213_out, not_214_out, not_215_out, A4, A2);
  and and_72 (and_72_out, not_216_out, not_217_out, A4, A2, not_218_out);
  and and_73 (and_73_out, not_219_out, not_220_out, A5, not_221_out, not_222_out, not_223_out);
  and and_74 (and_74_out, not_224_out, not_225_out, A5, not_226_out, not_227_out, A0);
  and and_75 (and_75_out, not_228_out, A5, not_229_out, not_230_out, A0);
  and and_76 (and_76_out, not_231_out, A5, not_232_out, not_233_out, not_234_out, A0);
  and and_77 (and_77_out, not_235_out, not_236_out, A5, not_237_out, A1, not_238_out);
  and and_78 (and_78_out, not_239_out, A5, not_240_out, A1, not_241_out);
  and and_79 (and_79_out, not_242_out, A5, not_243_out, not_244_out, A1, not_245_out);
  and and_80 (and_80_out, not_246_out, A5, not_247_out, not_248_out, A2, A1);
  and and_81 (and_81_out, not_249_out, A5, not_250_out, A3, not_251_out, not_252_out);
  and and_82 (and_82_out, not_253_out, A5, not_254_out, A3, not_255_out);
  and and_83 (and_83_out, not_256_out, A5, A3, A1, A0);
  and and_84 (and_84_out, not_257_out, A5, A4, A3, A2);
  and and_85 (and_85_out, A6, not_258_out, not_259_out, not_260_out, not_261_out, not_262_out);
  and and_86 (and_86_out, not_263_out, A6, not_264_out, not_265_out, A2);
  and and_87 (and_87_out, not_266_out, A6, not_267_out, A2, A0);
  and and_88 (and_88_out, A6, not_268_out, not_269_out, A2, A0);
  and and_89 (and_89_out, A6, not_270_out, A2, A1, A0);
  and and_90 (and_90_out, not_271_out, A6, not_272_out, A4, not_273_out);
  and and_91 (and_91_out, not_274_out, A6, A4, not_275_out, not_276_out);
  and and_92 (and_92_out, A6, not_277_out, A4, A2, not_278_out, not_279_out);
  and and_93 (and_93_out, not_280_out, A6, not_281_out, A4, A3, not_282_out);
  and and_94 (and_94_out, not_283_out, A6, not_284_out, A4, A3, not_285_out);
  and and_95 (and_95_out, not_286_out, A6, A5, not_287_out, not_288_out, A1);
  and and_96 (and_96_out, not_289_out, A6, A5, not_290_out, A2, A1);
  and and_97 (and_97_out, A6, A5, not_291_out, A2, A1);
  and and_98 (and_98_out, not_292_out, A6, A5, A3, not_293_out, not_294_out);
  and and_99 (and_99_out, A6, A5, A4, A3, not_295_out);
  and and_100 (and_100_out, A7, not_296_out, not_297_out, not_298_out, not_299_out);
  and and_101 (and_101_out, A7, not_300_out, not_301_out, not_302_out, A1, not_303_out);
  and and_102 (and_102_out, A7, not_304_out, not_305_out, A2, not_306_out, A0);
  and and_103 (and_103_out, A7, not_307_out, not_308_out, A3, not_309_out, A0);
  and and_104 (and_104_out, A7, not_310_out, not_311_out, not_312_out, A3, A1);
  and and_105 (and_105_out, A7, not_313_out, not_314_out, A3, A1, not_315_out);
  and and_106 (and_106_out, A7, not_316_out, not_317_out, A4, not_318_out, not_319_out, not_320_out);
  and and_107 (and_107_out, A7, not_321_out, A4, not_322_out, A2);
  and and_108 (and_108_out, A7, not_323_out, A4, A3, A2, A1);
  and and_109 (and_109_out, A7, A5, not_324_out, not_325_out, not_326_out, not_327_out);
  and and_110 (and_110_out, A7, not_328_out, A5, not_329_out, A1, A0);
  and and_111 (and_111_out, A7, A5, not_330_out, A1, A0);
  and and_112 (and_112_out, A7, not_331_out, A5, not_332_out, A3, not_333_out);
  and and_113 (and_113_out, A7, not_334_out, A5, A3, not_335_out, not_336_out);
  and and_114 (and_114_out, A7, A5, not_337_out, A3, not_338_out, A0);
  and and_115 (and_115_out, A7, A6, not_339_out, not_340_out, not_341_out, A0);
  and and_116 (and_116_out, A7, A6, not_342_out, not_343_out, A3, not_344_out, not_345_out);
  and and_117 (and_117_out, A7, A6, not_346_out, A3, not_347_out, not_348_out);
  and and_118 (and_118_out, A7, A6, not_349_out, A3, not_350_out, A1);
  and and_119 (and_119_out, A7, A6, not_351_out, A4, not_352_out, not_353_out);
  and and_120 (and_120_out, A7, A6, A4, not_354_out, not_355_out);
  and and_121 (and_121_out, A7, A6, A4, A3, A2, not_356_out);
  and and_122 (and_122_out, A7, A6, A5, not_357_out, not_358_out, not_359_out);
  and and_123 (and_123_out, A7, A6, A5, A4, A3, not_360_out);
  and and_124 (and_124_out, not_361_out, not_362_out, not_363_out, not_364_out);
  and and_125 (and_125_out, not_365_out, not_366_out, not_367_out, not_368_out, not_369_out);
  and and_126 (and_126_out, not_370_out, not_371_out, not_372_out, not_373_out, A2);
  and and_127 (and_127_out, not_374_out, not_375_out, A3, A1);
  and and_128 (and_128_out, not_376_out, not_377_out, A4, not_378_out);
  and and_129 (and_129_out, not_379_out, A4, not_380_out, not_381_out);
  and and_130 (and_130_out, not_382_out, not_383_out, A4, A2, not_384_out);
  and and_131 (and_131_out, not_385_out, not_386_out, A5, not_387_out, A1);
  and and_132 (and_132_out, not_388_out, A5, A3, not_389_out);
  and and_133 (and_133_out, not_390_out, A5, not_391_out, A3, A2);
  and and_134 (and_134_out, not_392_out, A5, A4, not_393_out, A1);
  and and_135 (and_135_out, not_394_out, A6, not_395_out, not_396_out, not_397_out);
  and and_136 (and_136_out, A6, not_398_out, not_399_out, A2);
  and and_137 (and_137_out, A6, not_400_out, A2, not_401_out);
  and and_138 (and_138_out, A6, not_402_out, A4, not_403_out, not_404_out);
  and and_139 (and_139_out, not_405_out, A6, A4, not_406_out, A2);
  and and_140 (and_140_out, A6, A5, not_407_out, not_408_out, A1);
  and and_141 (and_141_out, A6, A5, A4, A2, A1);
  and and_142 (and_142_out, A7, not_409_out, not_410_out, not_411_out, A1);
  and and_143 (and_143_out, A7, not_412_out, not_413_out, A1);
  and and_144 (and_144_out, A7, not_414_out, not_415_out, A3, not_416_out);
  and and_145 (and_145_out, A7, not_417_out, A3, A2, not_418_out);
  and and_146 (and_146_out, A7, not_419_out, A4, A3, A2);
  and and_147 (and_147_out, A7, not_420_out, A5, not_421_out, not_422_out);
  and and_148 (and_148_out, A7, A5, not_423_out, not_424_out);
  and and_149 (and_149_out, A7, A5, not_425_out, not_426_out, A2);
  and and_150 (and_150_out, A7, A5, A3, A1);
  and and_151 (and_151_out, A7, A6, A4, A3, not_427_out);
  and and_152 (and_152_out, not_428_out, not_429_out, not_430_out, not_431_out, not_432_out);
  and and_153 (and_153_out, not_433_out, not_434_out, not_435_out, not_436_out, not_437_out, A1);
  and and_154 (and_154_out, not_438_out, not_439_out, not_440_out, not_441_out, A1, not_442_out);
  and and_155 (and_155_out, not_443_out, not_444_out, not_445_out, A1, not_446_out);
  and and_156 (and_156_out, not_447_out, not_448_out, not_449_out, not_450_out, A1, not_451_out);
  and and_157 (and_157_out, not_452_out, not_453_out, not_454_out, not_455_out, A2, not_456_out, A0);
  and and_158 (and_158_out, not_457_out, not_458_out, not_459_out, not_460_out, A3, not_461_out);
  and and_159 (and_159_out, not_462_out, not_463_out, not_464_out, not_465_out, A3, A2, A0);
  and and_160 (and_160_out, not_466_out, not_467_out, not_468_out, A3, A2, not_469_out, A0);
  and and_161 (and_161_out, not_470_out, not_471_out, A4, not_472_out, not_473_out, not_474_out);
  and and_162 (and_162_out, not_475_out, not_476_out, not_477_out, A4, not_478_out, A1);
  and and_163 (and_163_out, not_479_out, not_480_out, A4, not_481_out, not_482_out, A1);
  and and_164 (and_164_out, not_483_out, not_484_out, A4, A2, not_485_out);
  and and_165 (and_165_out, not_486_out, A4, A2, not_487_out, not_488_out);
  and and_166 (and_166_out, not_489_out, not_490_out, A4, A3, not_491_out, not_492_out, A0);
  and and_167 (and_167_out, not_493_out, not_494_out, A4, A3, A2, not_495_out);
  and and_168 (and_168_out, not_496_out, not_497_out, A5, not_498_out, not_499_out, not_500_out);
  and and_169 (and_169_out, not_501_out, not_502_out, A5, not_503_out, not_504_out, not_505_out);
  and and_170 (and_170_out, not_506_out, A5, not_507_out, not_508_out, not_509_out);
  and and_171 (and_171_out, not_510_out, A5, not_511_out, not_512_out, not_513_out, not_514_out);
  and and_172 (and_172_out, not_515_out, A5, not_516_out, not_517_out, A1, A0);
  and and_173 (and_173_out, not_518_out, A5, not_519_out, not_520_out, A2, not_521_out);
  and and_174 (and_174_out, not_522_out, not_523_out, A5, A3, not_524_out, A1);
  and and_175 (and_175_out, not_525_out, A5, A3, A1, not_526_out);
  and and_176 (and_176_out, not_527_out, not_528_out, A5, A4, not_529_out, A2, A0);
  and and_177 (and_177_out, not_530_out, not_531_out, A5, A4, A3, A1);
  and and_178 (and_178_out, not_532_out, A5, A4, A3, not_533_out, A1);
  and and_179 (and_179_out, not_534_out, A6, not_535_out, not_536_out, not_537_out, not_538_out, A0);
  and and_180 (and_180_out, not_539_out, A6, not_540_out, A2, not_541_out);
  and and_181 (and_181_out, A6, not_542_out, not_543_out, A2, not_544_out);
  and and_182 (and_182_out, not_545_out, A6, not_546_out, not_547_out, A2, not_548_out, A0);
  and and_183 (and_183_out, not_549_out, A6, not_550_out, A3, not_551_out, not_552_out);
  and and_184 (and_184_out, not_553_out, A6, not_554_out, not_555_out, A3, A1, A0);
  and and_185 (and_185_out, A6, not_556_out, A4, not_557_out, not_558_out);
  and and_186 (and_186_out, A6, A4, not_559_out, not_560_out, not_561_out);
  and and_187 (and_187_out, not_562_out, A6, not_563_out, A4, A3, A2, A0);
  and and_188 (and_188_out, not_564_out, A6, A5, not_565_out, not_566_out, not_567_out);
  and and_189 (and_189_out, not_568_out, A6, A5, not_569_out, A2, A1);
  and and_190 (and_190_out, not_570_out, A6, A5, not_571_out, A3, not_572_out, A0);
  and and_191 (and_191_out, not_573_out, A6, A5, A3, A2, not_574_out, A0);
  and and_192 (and_192_out, not_575_out, A6, A5, A4, not_576_out, not_577_out, A0);
  and and_193 (and_193_out, A7, not_578_out, not_579_out, not_580_out, not_581_out, not_582_out);
  and and_194 (and_194_out, A7, not_583_out, not_584_out, not_585_out, not_586_out);
  and and_195 (and_195_out, A7, not_587_out, not_588_out, not_589_out, not_590_out, A0);
  and and_196 (and_196_out, A7, not_591_out, not_592_out, not_593_out, not_594_out, A2, A0);
  and and_197 (and_197_out, A7, not_595_out, not_596_out, not_597_out, A2, not_598_out, A0);
  and and_198 (and_198_out, A7, not_599_out, A3, not_600_out, not_601_out, not_602_out);
  and and_199 (and_199_out, A7, not_603_out, not_604_out, A3, not_605_out, A1);
  and and_200 (and_200_out, A7, not_606_out, not_607_out, A3, A1, not_608_out);
  and and_201 (and_201_out, A7, not_609_out, not_610_out, A3, A1, A0);
  and and_202 (and_202_out, A7, not_611_out, A4, A2, not_612_out);
  and and_203 (and_203_out, A7, not_613_out, A5, not_614_out, not_615_out, A1);
  and and_204 (and_204_out, A7, not_616_out, A5, not_617_out, A1, not_618_out);
  and and_205 (and_205_out, A7, A5, not_619_out, A1, not_620_out);
  and and_206 (and_206_out, A7, A5, not_621_out, A3, not_622_out, not_623_out);
  and and_207 (and_207_out, A7, not_624_out, A5, A3, not_625_out, A0);
  and and_208 (and_208_out, A7, not_626_out, A5, not_627_out, A3, A2, A0);
  and and_209 (and_209_out, A7, not_628_out, A5, A4, not_629_out, A1);
  and and_210 (and_210_out, A7, A5, A4, not_630_out, not_631_out, A1);
  and and_211 (and_211_out, A7, A6, not_632_out, not_633_out, not_634_out, not_635_out);
  and and_212 (and_212_out, A7, A6, not_636_out, not_637_out, not_638_out, A1, A0);
  and and_213 (and_213_out, A7, A6, not_639_out, not_640_out, A3, A2, not_641_out, A0);
  and and_214 (and_214_out, A7, A6, not_642_out, A4, not_643_out, not_644_out);
  and and_215 (and_215_out, A7, A6, not_645_out, A4, not_646_out, not_647_out);
  and and_216 (and_216_out, A7, A6, A4, not_648_out, not_649_out);
  and and_217 (and_217_out, A7, A6, not_650_out, A4, not_651_out, A2, A0);
  and and_218 (and_218_out, A7, A6, not_652_out, A4, A3, A1);
  and and_219 (and_219_out, A7, A6, A5, not_653_out, not_654_out, not_655_out, A0);
  and and_220 (and_220_out, A7, A6, A5, not_656_out, A2, not_657_out, A0);
  and and_221 (and_221_out, A7, A6, A5, not_658_out, A3, not_659_out, A0);
  and and_222 (and_222_out, A7, A6, A5, not_660_out, A3, A2, A1);
  and and_223 (and_223_out, A7, A6, A5, A4, A3, not_661_out);
  and and_224 (and_224_out, A7, A6, A5, A4, A3, A2, A0);
  and and_225 (and_225_out, not_662_out, not_663_out, not_664_out, not_665_out, not_666_out);
  and and_226 (and_226_out, not_667_out, not_668_out, not_669_out, not_670_out, A1, not_671_out);
  and and_227 (and_227_out, not_672_out, not_673_out, not_674_out, A1, not_675_out);
  and and_228 (and_228_out, not_676_out, not_677_out, not_678_out, not_679_out, A1, not_680_out);
  and and_229 (and_229_out, not_681_out, not_682_out, not_683_out, A3, not_684_out, not_685_out);
  and and_230 (and_230_out, not_686_out, not_687_out, A4, not_688_out, not_689_out, not_690_out);
  and and_231 (and_231_out, not_691_out, not_692_out, A4, A2, not_693_out);
  and and_232 (and_232_out, not_694_out, A4, A2, not_695_out, not_696_out);
  and and_233 (and_233_out, not_697_out, not_698_out, A5, not_699_out, not_700_out, not_701_out);
  and and_234 (and_234_out, not_702_out, A5, not_703_out, not_704_out, not_705_out);
  and and_235 (and_235_out, not_706_out, A5, not_707_out, not_708_out, not_709_out, not_710_out);
  and and_236 (and_236_out, not_711_out, A5, not_712_out, not_713_out, A2, not_714_out);
  and and_237 (and_237_out, not_715_out, A5, A3, A1, not_716_out);
  and and_238 (and_238_out, not_717_out, A6, not_718_out, A2, not_719_out);
  and and_239 (and_239_out, A6, not_720_out, not_721_out, A2, not_722_out);
  and and_240 (and_240_out, not_723_out, A6, not_724_out, A3, not_725_out, not_726_out);
  and and_241 (and_241_out, A6, not_727_out, A4, not_728_out, not_729_out);
  and and_242 (and_242_out, A6, A4, not_730_out, not_731_out, not_732_out);
  and and_243 (and_243_out, not_733_out, A6, A5, not_734_out, not_735_out, not_736_out);
  and and_244 (and_244_out, not_737_out, A6, A5, not_738_out, A2, not_739_out);
  and and_245 (and_245_out, A6, A5, not_740_out, A2, not_741_out);
  and and_246 (and_246_out, A7, not_742_out, not_743_out, not_744_out, not_745_out, not_746_out);
  and and_247 (and_247_out, A7, not_747_out, not_748_out, not_749_out, not_750_out);
  and and_248 (and_248_out, A7, not_751_out, not_752_out, not_753_out, not_754_out, not_755_out);
  and and_249 (and_249_out, A7, not_756_out, not_757_out, A3, not_758_out, not_759_out);
  and and_250 (and_250_out, A7, not_760_out, not_761_out, A3, A1, not_762_out);
  and and_251 (and_251_out, A7, not_763_out, A4, A2, not_764_out);
  and and_252 (and_252_out, A7, not_765_out, A5, not_766_out, A1, not_767_out);
  and and_253 (and_253_out, A7, A5, not_768_out, A1, not_769_out);
  and and_254 (and_254_out, A7, A5, not_770_out, A3, not_771_out, not_772_out);
  and and_255 (and_255_out, A7, A6, not_773_out, A4, not_774_out, not_775_out);
  and and_256 (and_256_out, A7, A6, A4, not_776_out, not_777_out);
  and and_257 (and_257_out, A7, A6, not_778_out, A4, A3, not_779_out);
  and and_258 (and_258_out, A7, A6, A5, A3, not_780_out, not_781_out);
  and and_259 (and_259_out, not_782_out, not_783_out, not_784_out, not_785_out, not_786_out);
  and and_260 (and_260_out, not_787_out, not_788_out, not_789_out, not_790_out, A2, not_791_out);
  and and_261 (and_261_out, not_792_out, not_793_out, not_794_out, not_795_out, A2, not_796_out);
  and and_262 (and_262_out, not_797_out, not_798_out, not_799_out, A3, not_800_out, not_801_out);
  and and_263 (and_263_out, not_802_out, not_803_out, A3, A1, not_804_out);
  and and_264 (and_264_out, not_805_out, not_806_out, not_807_out, A3, A2, A1);
  and and_265 (and_265_out, not_808_out, not_809_out, A4, not_810_out, not_811_out);
  and and_266 (and_266_out, not_812_out, not_813_out, not_814_out, A4, not_815_out, not_816_out, A1);
  and and_267 (and_267_out, not_817_out, not_818_out, A4, A2, not_819_out, not_820_out);
  and and_268 (and_268_out, not_821_out, not_822_out, not_823_out, A4, A3, not_824_out);
  and and_269 (and_269_out, not_825_out, not_826_out, A4, A3, not_827_out, not_828_out);
  and and_270 (and_270_out, not_829_out, not_830_out, A5, not_831_out, not_832_out, A1);
  and and_271 (and_271_out, not_833_out, A5, not_834_out, A2, A1, not_835_out);
  and and_272 (and_272_out, not_836_out, A5, A3, not_837_out, not_838_out);
  and and_273 (and_273_out, not_839_out, A5, not_840_out, A3, A2, not_841_out);
  and and_274 (and_274_out, not_842_out, not_843_out, A5, A4, not_844_out, not_845_out, not_846_out);
  and and_275 (and_275_out, not_847_out, A5, A4, not_848_out, A2, A1);
  and and_276 (and_276_out, not_849_out, not_850_out, A5, A4, A3, not_851_out, A1);
  and and_277 (and_277_out, not_852_out, A6, not_853_out, not_854_out, not_855_out, not_856_out);
  and and_278 (and_278_out, not_857_out, A6, not_858_out, not_859_out, not_860_out, not_861_out);
  and and_279 (and_279_out, not_862_out, A6, not_863_out, not_864_out, A2, not_865_out);
  and and_280 (and_280_out, A6, not_866_out, not_867_out, A2, not_868_out);
  and and_281 (and_281_out, A6, not_869_out, A2, not_870_out, not_871_out);
  and and_282 (and_282_out, not_872_out, A6, not_873_out, not_874_out, A3, A1);
  and and_283 (and_283_out, not_875_out, A6, not_876_out, A3, A2, A1);
  and and_284 (and_284_out, not_877_out, A6, A4, not_878_out, A2, not_879_out);
  and and_285 (and_285_out, not_880_out, A6, A5, not_881_out, not_882_out, A1);
  and and_286 (and_286_out, not_883_out, A6, A5, not_884_out, A3, not_885_out);
  and and_287 (and_287_out, not_886_out, A6, A5, not_887_out, A3, not_888_out);
  and and_288 (and_288_out, not_889_out, A6, A5, A3, A2, not_890_out);
  and and_289 (and_289_out, A6, A5, A4, A2, A1, not_891_out);
  and and_290 (and_290_out, A7, not_892_out, not_893_out, not_894_out, not_895_out, not_896_out);
  and and_291 (and_291_out, A7, not_897_out, not_898_out, A1, not_899_out);
  and and_292 (and_292_out, A7, not_900_out, not_901_out, not_902_out, A2, A1);
  and and_293 (and_293_out, A7, not_903_out, not_904_out, A3, not_905_out, not_906_out);
  and and_294 (and_294_out, A7, not_907_out, not_908_out, A3, not_909_out, A1);
  and and_295 (and_295_out, A7, not_910_out, not_911_out, A4, not_912_out, not_913_out);
  and and_296 (and_296_out, A7, not_914_out, A4, not_915_out, not_916_out, not_917_out);
  and and_297 (and_297_out, A7, not_918_out, not_919_out, A4, A3, A1);
  and and_298 (and_298_out, A7, not_920_out, A4, A3, not_921_out, A1);
  and and_299 (and_299_out, A7, A5, not_922_out, not_923_out, not_924_out);
  and and_300 (and_300_out, A7, A5, not_925_out, not_926_out, A2, not_927_out);
  and and_301 (and_301_out, A7, not_928_out, A5, A3, not_929_out, not_930_out);
  and and_302 (and_302_out, A7, A5, A3, A1, not_931_out);
  and and_303 (and_303_out, A7, A5, not_932_out, A3, A2, A1);
  and and_304 (and_304_out, A7, not_933_out, A5, A4, not_934_out, not_935_out, A1);
  and and_305 (and_305_out, A7, not_936_out, A5, A4, A3, not_937_out);
  and and_306 (and_306_out, A7, A5, A4, A3, not_938_out, not_939_out);
  and and_307 (and_307_out, A7, A6, not_940_out, not_941_out, not_942_out, A1);
  and and_308 (and_308_out, A7, A6, not_943_out, not_944_out, A2, A1);
  and and_309 (and_309_out, A7, A6, not_945_out, A3, not_946_out, not_947_out);
  and and_310 (and_310_out, A7, A6, not_948_out, not_949_out, A3, A2, not_950_out);
  and and_311 (and_311_out, A7, A6, A5, not_951_out, not_952_out, not_953_out);
  and and_312 (and_312_out, A7, A6, A5, not_954_out, not_955_out, not_956_out);
  and and_313 (and_313_out, A7, A6, A5, not_957_out, A2, not_958_out);
  and and_314 (and_314_out, A7, A6, A5, not_959_out, A3, A1);
  and and_315 (and_315_out, A7, A6, A5, A3, A2, A1);
  and and_316 (and_316_out, not_960_out, not_961_out, not_962_out, not_963_out, not_964_out, A1);
  and and_317 (and_317_out, not_965_out, not_966_out, not_967_out, not_968_out, A2, not_969_out);
  and and_318 (and_318_out, not_970_out, not_971_out, not_972_out, A2, not_973_out);
  and and_319 (and_319_out, not_974_out, not_975_out, not_976_out, A2, not_977_out);
  and and_320 (and_320_out, not_978_out, not_979_out, not_980_out, A3, not_981_out);
  and and_321 (and_321_out, not_982_out, not_983_out, A3, not_984_out, not_985_out);
  and and_322 (and_322_out, not_986_out, not_987_out, not_988_out, not_989_out, A3, A2);
  and and_323 (and_323_out, not_990_out, not_991_out, not_992_out, A3, A2, not_993_out);
  and and_324 (and_324_out, not_994_out, not_995_out, A4, not_996_out, not_997_out);
  and and_325 (and_325_out, not_998_out, A4, not_999_out, not_1000_out, not_1001_out);
  and and_326 (and_326_out, not_1002_out, not_1003_out, not_1004_out, A4, not_1005_out, A1);
  and and_327 (and_327_out, not_1006_out, not_1007_out, A4, not_1008_out, not_1009_out, A1);
  and and_328 (and_328_out, not_1010_out, not_1011_out, A5, not_1012_out, not_1013_out, not_1014_out);
  and and_329 (and_329_out, not_1015_out, A5, not_1016_out, not_1017_out, A1);
  and and_330 (and_330_out, not_1018_out, not_1019_out, A5, A3, not_1020_out, A1);
  and and_331 (and_331_out, not_1021_out, not_1022_out, A5, A4, not_1023_out, A2);
  and and_332 (and_332_out, not_1024_out, not_1025_out, A5, A4, A3, A1);
  and and_333 (and_333_out, not_1026_out, A6, not_1027_out, not_1028_out, not_1029_out, not_1030_out);
  and and_334 (and_334_out, not_1031_out, A6, not_1032_out, not_1033_out, not_1034_out);
  and and_335 (and_335_out, A6, not_1035_out, not_1036_out, A2, not_1037_out, not_1038_out);
  and and_336 (and_336_out, not_1039_out, A6, not_1040_out, not_1041_out, A3, A1);
  and and_337 (and_337_out, not_1042_out, A6, not_1043_out, A4, A2, not_1044_out);
  and and_338 (and_338_out, not_1045_out, A6, A4, A2, not_1046_out);
  and and_339 (and_339_out, A6, A4, not_1047_out, A2, not_1048_out);
  and and_340 (and_340_out, not_1049_out, A6, not_1050_out, A4, A3, A2);
  and and_341 (and_341_out, A6, A5, not_1051_out, not_1052_out, not_1053_out);
  and and_342 (and_342_out, not_1054_out, A6, A5, not_1055_out, A1);
  and and_343 (and_343_out, not_1056_out, A6, A5, not_1057_out, A3, not_1058_out);
  and and_344 (and_344_out, not_1059_out, A6, A5, A3, A2, not_1060_out);
  and and_345 (and_345_out, not_1061_out, A6, A5, A4, not_1062_out, not_1063_out);
  and and_346 (and_346_out, not_1064_out, A6, A5, A4, not_1065_out, A1);
  and and_347 (and_347_out, A7, not_1066_out, not_1067_out, not_1068_out, not_1069_out);
  and and_348 (and_348_out, A7, not_1070_out, not_1071_out, not_1072_out, not_1073_out, not_1074_out);
  and and_349 (and_349_out, A7, not_1075_out, not_1076_out, not_1077_out, not_1078_out);
  and and_350 (and_350_out, A7, not_1079_out, not_1080_out, not_1081_out, not_1082_out, A2);
  and and_351 (and_351_out, A7, not_1083_out, not_1084_out, A3, A1);
  and and_352 (and_352_out, A7, not_1085_out, A3, not_1086_out, A1);
  and and_353 (and_353_out, A7, not_1087_out, not_1088_out, A4, not_1089_out, not_1090_out);
  and and_354 (and_354_out, A7, not_1091_out, not_1092_out, A4, not_1093_out, not_1094_out);
  and and_355 (and_355_out, A7, not_1095_out, A4, not_1096_out, not_1097_out);
  and and_356 (and_356_out, A7, not_1098_out, A4, not_1099_out, not_1100_out, not_1101_out);
  and and_357 (and_357_out, A7, not_1102_out, A5, not_1103_out, not_1104_out, A1);
  and and_358 (and_358_out, A7, A5, not_1105_out, not_1106_out, A2, not_1107_out);
  and and_359 (and_359_out, A7, not_1108_out, A5, A3, not_1109_out);
  and and_360 (and_360_out, A7, A5, not_1110_out, A3, A2, A1);
  and and_361 (and_361_out, A7, not_1111_out, A5, A4, not_1112_out, A1);
  and and_362 (and_362_out, A7, A5, A4, not_1113_out, not_1114_out, A1);
  and and_363 (and_363_out, A7, A5, A4, A3, not_1115_out);
  and and_364 (and_364_out, A7, A6, not_1116_out, not_1117_out, not_1118_out, A1);
  and and_365 (and_365_out, A7, A6, not_1119_out, not_1120_out, A3, A2, not_1121_out);
  and and_366 (and_366_out, A7, A6, not_1122_out, A3, A2, not_1123_out);
  and and_367 (and_367_out, A7, A6, not_1124_out, A4, not_1125_out, A2);
  and and_368 (and_368_out, A7, A6, A4, A3, A2, A1);
  and and_369 (and_369_out, A7, A6, A5, not_1126_out, not_1127_out, not_1128_out);
  and and_370 (and_370_out, A7, A6, A5, not_1129_out, A2, not_1130_out);
  and and_371 (and_371_out, A7, A6, A5, not_1131_out, A3, not_1132_out);
  or or_1 (or_1_out, and_225_out, and_226_out, and_227_out, and_228_out, and_229_out, and_230_out, and_231_out, and_232_out, and_233_out, and_234_out, and_235_out, and_236_out, and_237_out, and_238_out, and_239_out, and_240_out, and_241_out);
  or or_2 (or_2_out, and_242_out, and_243_out, and_244_out, and_245_out, and_246_out, and_247_out, and_248_out, and_249_out, and_250_out, and_251_out, and_252_out, and_253_out, and_254_out, and_255_out, and_256_out, and_257_out, and_258_out);
  or or_3 (or_3_out, and_1_out, and_2_out, and_3_out, and_4_out, and_5_out, and_6_out, and_7_out, and_8_out, and_9_out, and_10_out, and_11_out, and_12_out, and_13_out, and_14_out, and_15_out, and_16_out, and_17_out, and_18_out, and_19_out, and_20_out, and_21_out, and_22_out, and_23_out, and_24_out, and_25_out, and_26_out, and_27_out, and_28_out, and_29_out, and_30_out);
  or or_4 (or_4_out, and_31_out, and_32_out, and_33_out, and_34_out, and_35_out, and_36_out, and_37_out, and_38_out, and_39_out, and_40_out, and_41_out, and_42_out, and_43_out, and_44_out, and_45_out, and_46_out, and_47_out, and_48_out, and_49_out, and_50_out, and_51_out, and_52_out, and_53_out, and_54_out, and_55_out, and_56_out, and_57_out, and_58_out, and_59_out, and_60_out);
  or or_5 (or_5_out, and_61_out, and_62_out, and_63_out, and_64_out, and_65_out, and_66_out, and_67_out, and_68_out, and_69_out, and_70_out, and_71_out, and_72_out, and_73_out, and_74_out, and_75_out, and_76_out, and_77_out, and_78_out, and_79_out, and_80_out, and_81_out, and_82_out, and_83_out, and_84_out, and_85_out, and_86_out, and_87_out, and_88_out, and_89_out, and_90_out, and_91_out, and_92_out);
  or or_6 (or_6_out, and_93_out, and_94_out, and_95_out, and_96_out, and_97_out, and_98_out, and_99_out, and_100_out, and_101_out, and_102_out, and_103_out, and_104_out, and_105_out, and_106_out, and_107_out, and_108_out, and_109_out, and_110_out, and_111_out, and_112_out, and_113_out, and_114_out, and_115_out, and_116_out, and_117_out, and_118_out, and_119_out, and_120_out, and_121_out, and_122_out, and_123_out);
  or or_7 (C, and_124_out, and_125_out, A0, and_126_out, and_127_out, and_128_out, and_129_out, and_130_out, and_131_out, and_132_out, and_133_out, and_134_out, and_135_out, and_136_out, and_137_out, and_138_out, and_139_out, and_140_out, and_141_out, and_142_out, and_143_out, and_144_out, and_145_out, and_146_out, and_147_out, and_148_out, and_149_out, and_150_out, and_151_out);
  or or_8 (or_8_out, and_152_out, and_153_out, and_154_out, and_155_out, and_156_out, and_157_out, and_158_out, and_159_out, and_160_out, and_161_out, and_162_out, and_163_out, and_164_out, and_165_out, and_166_out, and_167_out, and_168_out, and_169_out, and_170_out, and_171_out, and_172_out, and_173_out, and_174_out, and_175_out, and_176_out);
  or or_9 (or_9_out, and_177_out, and_178_out, and_179_out, and_180_out, and_181_out, and_182_out, and_183_out, and_184_out, and_185_out, and_186_out, and_187_out, and_188_out, and_189_out, and_190_out, and_191_out, and_192_out, and_193_out, and_194_out, and_195_out, and_196_out, and_197_out, and_198_out, and_199_out, and_200_out);
  or or_10 (or_10_out, and_201_out, and_202_out, and_203_out, and_204_out, and_205_out, and_206_out, and_207_out, and_208_out, and_209_out, and_210_out, and_211_out, and_212_out, and_213_out, and_214_out, and_215_out, and_216_out, and_217_out, and_218_out, and_219_out, and_220_out, and_221_out, and_222_out, and_223_out, and_224_out);
  or or_11 (E, or_1_out, or_2_out);
  or or_12 (or_12_out, and_259_out, and_260_out, and_261_out, and_262_out, and_263_out, and_264_out, and_265_out, and_266_out, and_267_out, and_268_out, and_269_out, and_270_out, and_271_out, and_272_out, and_273_out, and_274_out, and_275_out, and_276_out, and_277_out, and_278_out, and_279_out, and_280_out, and_281_out, and_282_out, and_283_out, and_284_out, and_285_out, and_286_out, and_287_out);
  or or_13 (or_13_out, and_288_out, and_289_out, and_290_out, and_291_out, and_292_out, and_293_out, and_294_out, and_295_out, and_296_out, and_297_out, and_298_out, and_299_out, and_300_out, and_301_out, and_302_out, and_303_out, and_304_out, and_305_out, and_306_out, and_307_out, and_308_out, and_309_out, and_310_out, and_311_out, and_312_out, and_313_out, and_314_out, and_315_out);
  or or_14 (or_14_out, and_316_out, and_317_out, and_318_out, and_319_out, and_320_out, and_321_out, and_322_out, and_323_out, and_324_out, and_325_out, and_326_out, and_327_out, and_328_out, and_329_out, and_330_out, and_331_out, and_332_out, and_333_out, and_334_out, and_335_out, and_336_out, and_337_out, and_338_out, and_339_out, and_340_out, and_341_out, and_342_out, and_343_out);
  or or_15 (or_15_out, and_344_out, and_345_out, and_346_out, and_347_out, and_348_out, and_349_out, and_350_out, and_351_out, and_352_out, and_353_out, and_354_out, and_355_out, and_356_out, and_357_out, and_358_out, and_359_out, and_360_out, and_361_out, and_362_out, and_363_out, and_364_out, and_365_out, and_366_out, and_367_out, and_368_out, and_369_out, and_370_out, and_371_out);
  or or_16 (A, or_3_out, or_4_out);
  or or_17 (B, or_5_out, or_6_out);
  or or_18 (D, or_8_out, or_9_out, or_10_out);
  or or_19 (F, or_12_out, or_13_out);
  or or_20 (G, or_14_out, or_15_out);

  // Notes on the sheet:
  //   DISPLAY UNIDADE
endmodule
module DisplayDezena (
  input  A7,
  input  A6,
  input  A5,
  input  A4,
  input  A3,
  input  A2,
  input  A1,
  input  A0,
  output A,
  output B,
  output C,
  output D,
  output E,
  output F,
  output G
);

  wire and_1_out, and_2_out, and_3_out, and_4_out, and_5_out, and_6_out, and_7_out, and_8_out, and_9_out,
       and_10_out, and_11_out, and_12_out, and_13_out, and_14_out, and_15_out, and_16_out, and_17_out,
       and_18_out, and_19_out, and_20_out, and_21_out, and_22_out, and_23_out, and_24_out, and_25_out,
       and_26_out, and_27_out, and_28_out, and_29_out, and_30_out, and_31_out, and_32_out, and_33_out,
       and_34_out, and_35_out, and_36_out, and_37_out, and_38_out, and_39_out, and_40_out, and_41_out,
       and_42_out, and_43_out, and_44_out, and_45_out, and_46_out, and_47_out, and_48_out, and_49_out,
       and_50_out, and_51_out, and_52_out, and_53_out, and_54_out, and_55_out, and_56_out, and_57_out,
       and_58_out, and_59_out, and_60_out, and_61_out, and_62_out, and_63_out, and_64_out, and_65_out,
       and_66_out, and_67_out, and_68_out, and_69_out, and_70_out, and_71_out, and_72_out, and_73_out,
       and_74_out, and_75_out, and_76_out, and_77_out, and_78_out, and_79_out, and_80_out, and_81_out,
       and_82_out, and_83_out, and_84_out, and_85_out, and_86_out, and_87_out, and_88_out, and_89_out,
       and_90_out, and_91_out, and_92_out, and_93_out, and_94_out, and_95_out, and_96_out, and_97_out,
       and_98_out, and_99_out, and_100_out, and_101_out, and_102_out, and_103_out, and_104_out, and_105_out,
       and_106_out, and_107_out, and_108_out, and_109_out, and_110_out, and_111_out, and_112_out,
       and_113_out, and_114_out, and_115_out, and_116_out, not_1_out, not_2_out, not_3_out, not_4_out,
       not_5_out, not_6_out, not_7_out, not_8_out, not_9_out, not_10_out, not_11_out, not_12_out, not_13_out,
       not_14_out, not_15_out, not_16_out, not_17_out, not_18_out, not_19_out, not_20_out, not_21_out,
       not_22_out, not_23_out, not_24_out, not_25_out, not_26_out, not_27_out, not_28_out, not_29_out,
       not_30_out, not_31_out, not_32_out, not_33_out, not_34_out, not_35_out, not_36_out, not_37_out,
       not_38_out, not_39_out, not_40_out, not_41_out, not_42_out, not_43_out, not_44_out, not_45_out,
       not_46_out, not_47_out, not_48_out, not_49_out, not_50_out, not_51_out, not_52_out, not_53_out,
       not_54_out, not_55_out, not_56_out, not_57_out, not_58_out, not_59_out, not_60_out, not_61_out,
       not_62_out, not_63_out, not_64_out, not_65_out, not_66_out, not_67_out, not_68_out, not_69_out,
       not_70_out, not_71_out, not_72_out, not_73_out, not_74_out, not_75_out, not_76_out, not_77_out,
       not_78_out, not_79_out, not_80_out, not_81_out, not_82_out, not_83_out, not_84_out, not_85_out,
       not_86_out, not_87_out, not_88_out, not_89_out, not_90_out, not_91_out, not_92_out, not_93_out,
       not_94_out, not_95_out, not_96_out, not_97_out, not_98_out, not_99_out, not_100_out, not_101_out,
       not_102_out, not_103_out, not_104_out, not_105_out, not_106_out, not_107_out, not_108_out,
       not_109_out, not_110_out, not_111_out, not_112_out, not_113_out, not_114_out, not_115_out,
       not_116_out, not_117_out, not_118_out, not_119_out, not_120_out, not_121_out, not_122_out,
       not_123_out, not_124_out, not_125_out, not_126_out, not_127_out, not_128_out, not_129_out,
       not_130_out, not_131_out, not_132_out, not_133_out, not_134_out, not_135_out, not_136_out,
       not_137_out, not_138_out, not_139_out, not_140_out, not_141_out, not_142_out, not_143_out,
       not_144_out, not_145_out, not_146_out, not_147_out, not_148_out, not_149_out, not_150_out,
       not_151_out, not_152_out, not_153_out, not_154_out, not_155_out, not_156_out, not_157_out,
       not_158_out, not_159_out, not_160_out, not_161_out, not_162_out, not_163_out, not_164_out,
       not_165_out, not_166_out, not_167_out, not_168_out, not_169_out, not_170_out, not_171_out,
       not_172_out, not_173_out, not_174_out, not_175_out, not_176_out, not_177_out, not_178_out,
       not_179_out, not_180_out, not_181_out, not_182_out, not_183_out, not_184_out, not_185_out,
       not_186_out, not_187_out, not_188_out, not_189_out, not_190_out, not_191_out, not_192_out,
       not_193_out, not_194_out, not_195_out, not_196_out, not_197_out, not_198_out, not_199_out,
       not_200_out, not_201_out, not_202_out, not_203_out, not_204_out, not_205_out, not_206_out,
       not_207_out, not_208_out, not_209_out, not_210_out, not_211_out, not_212_out, not_213_out,
       not_214_out, not_215_out, not_216_out, not_217_out, not_218_out, not_219_out, not_220_out,
       not_221_out, not_222_out, not_223_out, not_224_out, not_225_out, not_226_out, not_227_out,
       not_228_out, not_229_out, not_230_out, not_231_out, not_232_out, not_233_out, not_234_out,
       not_235_out, not_236_out, not_237_out, not_238_out, not_239_out, not_240_out, not_241_out,
       not_242_out, not_243_out, not_244_out, not_245_out, not_246_out, not_247_out, not_248_out,
       not_249_out, not_250_out, not_251_out, not_252_out, not_253_out, not_254_out, not_255_out,
       not_256_out, not_257_out, not_258_out, not_259_out, not_260_out, not_261_out, not_262_out,
       not_263_out, not_264_out, not_265_out, not_266_out, not_267_out, not_268_out;

  not not_1 (not_1_out, A5);
  not not_2 (not_2_out, A4);
  not not_3 (not_3_out, A2);
  not not_4 (not_4_out, A1);
  not not_5 (not_5_out, A4);
  not not_6 (not_6_out, A3);
  not not_7 (not_7_out, A7);
  not not_8 (not_8_out, A6);
  not not_9 (not_9_out, A3);
  not not_10 (not_10_out, A6);
  not not_11 (not_11_out, A3);
  not not_12 (not_12_out, A6);
  not not_13 (not_13_out, A6);
  not not_14 (not_14_out, A3);
  not not_15 (not_15_out, A7);
  not not_16 (not_16_out, A5);
  not not_17 (not_17_out, A5);
  not not_18 (not_18_out, A3);
  not not_19 (not_19_out, A2);
  not not_20 (not_20_out, A1);
  not not_21 (not_21_out, A4);
  not not_22 (not_22_out, A1);
  not not_23 (not_23_out, A7);
  not not_24 (not_24_out, A2);
  not not_25 (not_25_out, A4);
  not not_26 (not_26_out, A2);
  not not_27 (not_27_out, A6);
  not not_28 (not_28_out, A4);
  not not_29 (not_29_out, A6);
  not not_30 (not_30_out, A5);
  not not_31 (not_31_out, A4);
  not not_32 (not_32_out, A6);
  not not_33 (not_33_out, A5);
  not not_34 (not_34_out, A3);
  not not_35 (not_35_out, A2);
  not not_36 (not_36_out, A6);
  not not_37 (not_37_out, A5);
  not not_38 (not_38_out, A3);
  not not_39 (not_39_out, A1);
  not not_40 (not_40_out, A5);
  not not_41 (not_41_out, A4);
  not not_42 (not_42_out, A4);
  not not_43 (not_43_out, A4);
  not not_44 (not_44_out, A7);
  not not_45 (not_45_out, A5);
  not not_46 (not_46_out, A3);
  not not_47 (not_47_out, A2);
  not not_48 (not_48_out, A1);
  not not_49 (not_49_out, A7);
  not not_50 (not_50_out, A4);
  not not_51 (not_51_out, A4);
  not not_52 (not_52_out, A7);
  not not_53 (not_53_out, A3);
  not not_54 (not_54_out, A2);
  not not_55 (not_55_out, A1);
  not not_56 (not_56_out, A6);
  not not_57 (not_57_out, A5);
  not not_58 (not_58_out, A7);
  not not_59 (not_59_out, A4);
  not not_60 (not_60_out, A7);
  not not_61 (not_61_out, A3);
  not not_62 (not_62_out, A2);
  not not_63 (not_63_out, A5);
  not not_64 (not_64_out, A4);
  not not_65 (not_65_out, A4);
  not not_66 (not_66_out, A4);
  not not_67 (not_67_out, A6);
  not not_68 (not_68_out, A6);
  not not_69 (not_69_out, A7);
  not not_70 (not_70_out, A5);
  not not_71 (not_71_out, A7);
  not not_72 (not_72_out, A3);
  not not_73 (not_73_out, A5);
  not not_74 (not_74_out, A4);
  not not_75 (not_75_out, A6);
  not not_76 (not_76_out, A2);
  not not_77 (not_77_out, A3);
  not not_78 (not_78_out, A6);
  not not_79 (not_79_out, A5);
  not not_80 (not_80_out, A4);
  not not_81 (not_81_out, A2);
  not not_82 (not_82_out, A1);
  not not_83 (not_83_out, A6);
  not not_84 (not_84_out, A4);
  not not_85 (not_85_out, A3);
  not not_86 (not_86_out, A4);
  not not_87 (not_87_out, A3);
  not not_88 (not_88_out, A2);
  not not_89 (not_89_out, A4);
  not not_90 (not_90_out, A3);
  not not_91 (not_91_out, A1);
  not not_92 (not_92_out, A7);
  not not_93 (not_93_out, A6);
  not not_94 (not_94_out, A3);
  not not_95 (not_95_out, A6);
  not not_96 (not_96_out, A3);
  not not_97 (not_97_out, A6);
  not not_98 (not_98_out, A4);
  not not_99 (not_99_out, A3);
  not not_100 (not_100_out, A7);
  not not_101 (not_101_out, A6);
  not not_102 (not_102_out, A3);
  not not_103 (not_103_out, A6);
  not not_104 (not_104_out, A3);
  not not_105 (not_105_out, A5);
  not not_106 (not_106_out, A3);
  not not_107 (not_107_out, A2);
  not not_108 (not_108_out, A1);
  not not_109 (not_109_out, A7);
  not not_110 (not_110_out, A5);
  not not_111 (not_111_out, A4);
  not not_112 (not_112_out, A1);
  not not_113 (not_113_out, A7);
  not not_114 (not_114_out, A2);
  not not_115 (not_115_out, A5);
  not not_116 (not_116_out, A4);
  not not_117 (not_117_out, A2);
  not not_118 (not_118_out, A4);
  not not_119 (not_119_out, A2);
  not not_120 (not_120_out, A1);
  not not_121 (not_121_out, A4);
  not not_122 (not_122_out, A7);
  not not_123 (not_123_out, A6);
  not not_124 (not_124_out, A5);
  not not_125 (not_125_out, A4);
  not not_126 (not_126_out, A2);
  not not_127 (not_127_out, A1);
  not not_128 (not_128_out, A7);
  not not_129 (not_129_out, A5);
  not not_130 (not_130_out, A4);
  not not_131 (not_131_out, A3);
  not not_132 (not_132_out, A2);
  not not_133 (not_133_out, A6);
  not not_134 (not_134_out, A5);
  not not_135 (not_135_out, A4);
  not not_136 (not_136_out, A3);
  not not_137 (not_137_out, A2);
  not not_138 (not_138_out, A1);
  not not_139 (not_139_out, A7);
  not not_140 (not_140_out, A6);
  not not_141 (not_141_out, A5);
  not not_142 (not_142_out, A3);
  not not_143 (not_143_out, A7);
  not not_144 (not_144_out, A5);
  not not_145 (not_145_out, A3);
  not not_146 (not_146_out, A1);
  not not_147 (not_147_out, A7);
  not not_148 (not_148_out, A6);
  not not_149 (not_149_out, A5);
  not not_150 (not_150_out, A2);
  not not_151 (not_151_out, A7);
  not not_152 (not_152_out, A6);
  not not_153 (not_153_out, A5);
  not not_154 (not_154_out, A1);
  not not_155 (not_155_out, A7);
  not not_156 (not_156_out, A7);
  not not_157 (not_157_out, A5);
  not not_158 (not_158_out, A3);
  not not_159 (not_159_out, A7);
  not not_160 (not_160_out, A5);
  not not_161 (not_161_out, A2);
  not not_162 (not_162_out, A1);
  not not_163 (not_163_out, A5);
  not not_164 (not_164_out, A3);
  not not_165 (not_165_out, A2);
  not not_166 (not_166_out, A1);
  not not_167 (not_167_out, A7);
  not not_168 (not_168_out, A4);
  not not_169 (not_169_out, A3);
  not not_170 (not_170_out, A7);
  not not_171 (not_171_out, A2);
  not not_172 (not_172_out, A7);
  not not_173 (not_173_out, A1);
  not not_174 (not_174_out, A6);
  not not_175 (not_175_out, A4);
  not not_176 (not_176_out, A2);
  not not_177 (not_177_out, A1);
  not not_178 (not_178_out, A4);
  not not_179 (not_179_out, A3);
  not not_180 (not_180_out, A2);
  not not_181 (not_181_out, A4);
  not not_182 (not_182_out, A3);
  not not_183 (not_183_out, A1);
  not not_184 (not_184_out, A6);
  not not_185 (not_185_out, A3);
  not not_186 (not_186_out, A6);
  not not_187 (not_187_out, A2);
  not not_188 (not_188_out, A6);
  not not_189 (not_189_out, A1);
  not not_190 (not_190_out, A5);
  not not_191 (not_191_out, A4);
  not not_192 (not_192_out, A5);
  not not_193 (not_193_out, A7);
  not not_194 (not_194_out, A6);
  not not_195 (not_195_out, A5);
  not not_196 (not_196_out, A4);
  not not_197 (not_197_out, A3);
  not not_198 (not_198_out, A7);
  not not_199 (not_199_out, A6);
  not not_200 (not_200_out, A5);
  not not_201 (not_201_out, A4);
  not not_202 (not_202_out, A2);
  not not_203 (not_203_out, A1);
  not not_204 (not_204_out, A7);
  not not_205 (not_205_out, A5);
  not not_206 (not_206_out, A4);
  not not_207 (not_207_out, A3);
  not not_208 (not_208_out, A2);
  not not_209 (not_209_out, A7);
  not not_210 (not_210_out, A5);
  not not_211 (not_211_out, A4);
  not not_212 (not_212_out, A3);
  not not_213 (not_213_out, A1);
  not not_214 (not_214_out, A7);
  not not_215 (not_215_out, A6);
  not not_216 (not_216_out, A6);
  not not_217 (not_217_out, A2);
  not not_218 (not_218_out, A1);
  not not_219 (not_219_out, A7);
  not not_220 (not_220_out, A6);
  not not_221 (not_221_out, A5);
  not not_222 (not_222_out, A3);
  not not_223 (not_223_out, A2);
  not not_224 (not_224_out, A1);
  not not_225 (not_225_out, A7);
  not not_226 (not_226_out, A5);
  not not_227 (not_227_out, A7);
  not not_228 (not_228_out, A4);
  not not_229 (not_229_out, A3);
  not not_230 (not_230_out, A7);
  not not_231 (not_231_out, A4);
  not not_232 (not_232_out, A2);
  not not_233 (not_233_out, A7);
  not not_234 (not_234_out, A4);
  not not_235 (not_235_out, A1);
  not not_236 (not_236_out, A5);
  not not_237 (not_237_out, A4);
  not not_238 (not_238_out, A6);
  not not_239 (not_239_out, A5);
  not not_240 (not_240_out, A6);
  not not_241 (not_241_out, A6);
  not not_242 (not_242_out, A6);
  not not_243 (not_243_out, A4);
  not not_244 (not_244_out, A3);
  not not_245 (not_245_out, A5);
  not not_246 (not_246_out, A4);
  not not_247 (not_247_out, A6);
  not not_248 (not_248_out, A7);
  not not_249 (not_249_out, A6);
  not not_250 (not_250_out, A7);
  not not_251 (not_251_out, A6);
  not not_252 (not_252_out, A5);
  not not_253 (not_253_out, A4);
  not not_254 (not_254_out, A3);
  not not_255 (not_255_out, A1);
  not not_256 (not_256_out, A4);
  not not_257 (not_257_out, A3);
  not not_258 (not_258_out, A2);
  not not_259 (not_259_out, A7);
  not not_260 (not_260_out, A5);
  not not_261 (not_261_out, A6);
  not not_262 (not_262_out, A5);
  not not_263 (not_263_out, A6);
  not not_264 (not_264_out, A4);
  not not_265 (not_265_out, A2);
  not not_266 (not_266_out, A1);
  not not_267 (not_267_out, A4);
  not not_268 (not_268_out, A3);
  and and_1 (and_1_out, not_1_out, not_2_out, not_3_out, not_4_out);
  and and_2 (and_2_out, not_5_out, not_6_out);
  and and_3 (and_3_out, not_7_out, not_8_out, not_9_out, A2);
  and and_4 (and_4_out, not_10_out, not_11_out, A2, A1);
  and and_5 (and_5_out, not_12_out, A4, A3);
  and and_6 (and_6_out, A4, A3, A2);
  and and_7 (and_7_out, not_13_out, A5, not_14_out, A1);
  and and_8 (and_8_out, A5, A4, A3, A1);
  and and_9 (and_9_out, not_15_out, A6, not_16_out);
  and and_10 (and_10_out, A6, not_17_out, not_18_out, not_19_out, not_20_out);
  and and_11 (and_11_out, A6, not_21_out, not_22_out);
  and and_12 (and_12_out, not_23_out, A6, A3, not_24_out);
  and and_13 (and_13_out, A7, not_25_out, not_26_out);
  and and_14 (and_14_out, A7, not_27_out, A5);
  and and_15 (and_15_out, A7, A6, not_28_out);
  and and_16 (and_16_out, not_29_out, not_30_out, not_31_out);
  and and_17 (and_17_out, not_32_out, not_33_out, not_34_out, not_35_out);
  and and_18 (and_18_out, not_36_out, not_37_out, not_38_out, not_39_out);
  and and_19 (and_19_out, not_40_out, not_41_out, A2, A1);
  and and_20 (and_20_out, not_42_out, A3, A1);
  and and_21 (and_21_out, not_43_out, A3, A2);
  and and_22 (and_22_out, not_44_out, not_45_out, A4);
  and and_23 (and_23_out, A4, not_46_out, not_47_out, not_48_out);
  and and_24 (and_24_out, not_49_out, A5, not_50_out);
  and and_25 (and_25_out, A6, not_51_out, A3);
  and and_26 (and_26_out, not_52_out, A6, A4);
  and and_27 (and_27_out, A6, A5, not_53_out);
  and and_28 (and_28_out, A6, A5, not_54_out, not_55_out);
  and and_29 (and_29_out, A7, not_56_out, A5, A4);
  and and_30 (and_30_out, A7, A6, not_57_out);
  and and_31 (and_31_out, not_58_out, not_59_out);
  and and_32 (and_32_out, not_60_out, not_61_out, not_62_out);
  and and_33 (and_33_out, not_63_out, not_64_out, A1);
  and and_34 (and_34_out, not_65_out, A2, A1);
  and and_35 (and_35_out, not_66_out, A3);
  and and_36 (and_36_out, not_67_out, A3, A2, A1);
  and and_37 (and_37_out, not_68_out, A5);
  and and_38 (and_38_out, not_69_out, A6, not_70_out);
  and and_39 (and_39_out, not_71_out, A6, not_72_out);
  and and_40 (and_40_out, A6, not_73_out, not_74_out);
  and and_41 (and_41_out, A7, not_75_out, A2);
  and and_42 (and_42_out, A7, A3, not_76_out);
  and and_43 (and_43_out, A7, A4, not_77_out);
  and and_44 (and_44_out, A7, A5, A4);
  and and_45 (and_45_out, not_78_out, not_79_out, not_80_out, not_81_out, not_82_out);
  and and_46 (and_46_out, not_83_out, not_84_out, not_85_out);
  and and_47 (and_47_out, not_86_out, not_87_out, not_88_out);
  and and_48 (and_48_out, not_89_out, not_90_out, not_91_out);
  and and_49 (and_49_out, not_92_out, not_93_out, not_94_out, A2);
  and and_50 (and_50_out, not_95_out, not_96_out, A2, A1);
  and and_51 (and_51_out, not_97_out, A4, A3);
  and and_52 (and_52_out, A4, A3, A2);
  and and_53 (and_53_out, A5, not_98_out, not_99_out);
  and and_54 (and_54_out, not_100_out, not_101_out, A5, not_102_out, A1);
  and and_55 (and_55_out, not_103_out, A5, not_104_out, A2);
  and and_56 (and_56_out, A5, A4, A3, A1);
  and and_57 (and_57_out, A6, not_105_out, not_106_out, not_107_out, not_108_out);
  and and_58 (and_58_out, not_109_out, A6, not_110_out, A4);
  and and_59 (and_59_out, A6, A5, not_111_out, not_112_out);
  and and_60 (and_60_out, not_113_out, A6, A5, A3, not_114_out);
  and and_61 (and_61_out, A7, not_115_out, not_116_out, not_117_out);
  and and_62 (and_62_out, A7, not_118_out, not_119_out, not_120_out);
  and and_63 (and_63_out, A7, A6, not_121_out);
  and and_64 (and_64_out, not_122_out, not_123_out, not_124_out, not_125_out, not_126_out, not_127_out);
  and and_65 (and_65_out, not_128_out, not_129_out, not_130_out, not_131_out, not_132_out);
  and and_66 (and_66_out, not_133_out, not_134_out, not_135_out, not_136_out, not_137_out, not_138_out);
  and and_67 (and_67_out, not_139_out, not_140_out, not_141_out, not_142_out, A2);
  and and_68 (and_68_out, not_143_out, not_144_out, not_145_out, A2, not_146_out);
  and and_69 (and_69_out, not_147_out, not_148_out, not_149_out, A4, A3, not_150_out);
  and and_70 (and_70_out, not_151_out, not_152_out, not_153_out, A4, A3, not_154_out);
  and and_71 (and_71_out, not_155_out, A5, A4, A3, A2);
  and and_72 (and_72_out, not_156_out, A6, not_157_out, A4, not_158_out);
  and and_73 (and_73_out, not_159_out, A6, not_160_out, A4, not_161_out, not_162_out);
  and and_74 (and_74_out, A6, not_163_out, A4, not_164_out, not_165_out, not_166_out);
  and and_75 (and_75_out, not_167_out, A6, A5, not_168_out, not_169_out, A2);
  and and_76 (and_76_out, not_170_out, A6, A5, A3, not_171_out);
  and and_77 (and_77_out, not_172_out, A6, A5, A3, not_173_out);
  and and_78 (and_78_out, A7, not_174_out, A5, not_175_out, not_176_out, not_177_out);
  and and_79 (and_79_out, A7, A5, not_178_out, not_179_out, not_180_out);
  and and_80 (and_80_out, A7, A5, not_181_out, not_182_out, not_183_out);
  and and_81 (and_81_out, A7, not_184_out, A5, not_185_out, A2);
  and and_82 (and_82_out, A7, not_186_out, A5, A4, A3, not_187_out);
  and and_83 (and_83_out, A7, not_188_out, A5, A4, A3, not_189_out);
  and and_84 (and_84_out, A7, A6, not_190_out, not_191_out, A3);
  and and_85 (and_85_out, A7, A6, not_192_out, A3, A2);
  and and_86 (and_86_out, not_193_out, not_194_out, not_195_out, not_196_out, not_197_out);
  and and_87 (and_87_out, not_198_out, not_199_out, not_200_out, not_201_out, not_202_out, not_203_out);
  and and_88 (and_88_out, not_204_out, not_205_out, not_206_out, not_207_out, not_208_out);
  and and_89 (and_89_out, not_209_out, not_210_out, not_211_out, not_212_out, not_213_out);
  and and_90 (and_90_out, not_214_out, not_215_out, A5, A3);
  and and_91 (and_91_out, not_216_out, A5, A3, not_217_out, not_218_out);
  and and_92 (and_92_out, not_219_out, not_220_out, A5, A4);
  and and_93 (and_93_out, A6, not_221_out, not_222_out, not_223_out, not_224_out);
  and and_94 (and_94_out, not_225_out, A6, not_226_out, A4);
  and and_95 (and_95_out, not_227_out, A6, A5, not_228_out, not_229_out);
  and and_96 (and_96_out, not_230_out, A6, A5, not_231_out, not_232_out);
  and and_97 (and_97_out, not_233_out, A6, A5, not_234_out, not_235_out);
  and and_98 (and_98_out, A7, not_236_out, not_237_out, A3, A2);
  and and_99 (and_99_out, A7, not_238_out, not_239_out, A4);
  and and_100 (and_100_out, A7, not_240_out, A4, A2);
  and and_101 (and_101_out, A7, not_241_out, A4, A3);
  and and_102 (and_102_out, A7, not_242_out, A5, not_243_out, not_244_out);
  and and_103 (and_103_out, A7, A6, not_245_out, not_246_out);
  and and_104 (and_104_out, A7, A6, A5, A4);
  and and_105 (and_105_out, not_247_out, A4, A2);
  and and_106 (and_106_out, not_248_out, A4, A3);
  and and_107 (and_107_out, not_249_out, A4, A3);
  and and_108 (and_108_out, A4, A3, A2);
  and and_109 (and_109_out, not_250_out, not_251_out, A5);
  and and_110 (and_110_out, A6, not_252_out, not_253_out, not_254_out, not_255_out);
  and and_111 (and_111_out, A6, not_256_out, not_257_out, not_258_out);
  and and_112 (and_112_out, not_259_out, A6, not_260_out, A4);
  and and_113 (and_113_out, A7, not_261_out, not_262_out);
  and and_114 (and_114_out, A7, not_263_out, not_264_out, not_265_out, not_266_out);
  and and_115 (and_115_out, A7, not_267_out, not_268_out);
  and and_116 (and_116_out, A7, A6, A5);
  or or_1 (A, and_1_out, and_2_out, and_3_out, and_4_out, and_5_out, and_6_out, and_7_out, and_8_out, and_9_out, and_10_out, and_11_out, and_12_out, and_13_out, and_14_out, and_15_out);
  or or_2 (B, and_16_out, and_17_out, and_18_out, and_19_out, and_20_out, and_21_out, and_22_out, and_23_out, and_24_out, and_25_out, and_26_out, and_27_out, and_28_out, and_29_out, and_30_out);
  or or_3 (C, and_31_out, and_32_out, and_33_out, and_34_out, and_35_out, and_36_out, and_37_out, and_38_out, and_39_out, and_40_out, and_41_out, and_42_out, and_43_out, and_44_out);
  or or_4 (D, and_45_out, and_46_out, and_47_out, and_48_out, and_49_out, and_50_out, and_51_out, and_52_out, and_53_out, and_54_out, and_55_out, and_56_out, and_57_out, and_58_out, and_59_out, and_60_out, and_61_out, and_62_out, and_63_out);
  or or_5 (G, and_105_out, and_106_out, and_107_out, and_108_out, and_109_out, and_110_out, and_111_out, and_112_out, and_113_out, and_114_out, and_115_out, and_116_out);
  or or_6 (E, and_64_out, and_65_out, and_66_out, and_67_out, and_68_out, and_69_out, and_70_out, and_71_out, and_72_out, and_73_out, and_74_out, and_75_out, and_76_out, and_77_out, and_78_out, and_79_out, and_80_out, and_81_out, and_82_out, and_83_out, and_84_out, and_85_out);
  or or_7 (F, and_86_out, and_87_out, and_88_out, and_89_out, and_90_out, and_91_out, and_92_out, and_93_out, and_94_out, and_95_out, and_96_out, and_97_out, and_98_out, and_99_out, and_100_out, and_101_out, and_102_out, and_103_out, and_104_out);

  // Notes on the sheet:
  //   DISPLAY DEZENA
endmodule

module DisplayCentena (
  input  A7,
  input  A6,
  input  A5,
  input  A4,
  input  A3,
  input  A2,
  input  A1,
  input  A0,
  output A,
  output B,
  output C,
  output D,
  output E,
  output F,
  output G
);

  wire and_1_out, and_2_out, and_3_out, and_4_out, and_5_out, and_6_out, and_7_out, and_8_out, and_9_out,
       and_10_out, and_11_out, and_12_out, and_13_out, and_14_out, and_15_out, and_16_out, and_17_out,
       and_18_out, and_19_out, and_20_out, and_21_out, and_22_out, and_23_out, and_24_out, and_25_out,
       not_1_out, not_2_out, not_3_out, not_4_out, not_5_out, not_6_out, not_7_out, not_8_out, not_9_out,
       not_10_out, not_11_out, not_12_out, not_13_out, not_14_out, not_15_out, not_16_out, not_17_out,
       not_18_out, not_19_out, not_20_out, not_21_out, not_22_out, not_23_out, not_24_out, not_25_out,
       not_26_out, not_27_out, not_28_out, not_29_out, not_30_out, not_31_out, not_32_out, not_33_out,
       not_34_out, not_35_out, not_36_out, not_37_out, not_38_out, not_39_out, not_40_out, not_41_out,
       not_42_out, not_43_out;

  not not_1 (not_1_out, A7);
  not not_2 (not_2_out, A6);
  not not_3 (not_3_out, A7);
  not not_4 (not_4_out, A5);
  not not_5 (not_5_out, A7);
  not not_6 (not_6_out, A4);
  not not_7 (not_7_out, A3);
  not not_8 (not_8_out, A2);
  not not_9 (not_9_out, A5);
  not not_10 (not_10_out, A5);
  not not_11 (not_11_out, A7);
  not not_12 (not_12_out, A6);
  not not_13 (not_13_out, A5);
  and and_1 (and_1_out, not_13_out, not_14_out, not_15_out);
  not not_14 (not_14_out, A4);
  not not_15 (not_15_out, A3);
  not not_16 (not_16_out, A7);
  not not_17 (not_17_out, A6);
  not not_18 (not_18_out, A7);
  not not_19 (not_19_out, A5);
  not not_20 (not_20_out, A7);
  not not_21 (not_21_out, A4);
  not not_22 (not_22_out, A3);
  not not_23 (not_23_out, A2);
  not not_24 (not_24_out, A5);
  not not_25 (not_25_out, A5);
  not not_26 (not_26_out, A7);
  not not_27 (not_27_out, A6);
  not not_28 (not_28_out, A7);
  not not_29 (not_29_out, A5);
  not not_30 (not_30_out, A7);
  not not_31 (not_31_out, A4);
  not not_32 (not_32_out, A3);
  not not_33 (not_33_out, A2);
  not not_34 (not_34_out, A5);
  not not_35 (not_35_out, A5);
  not not_36 (not_36_out, A7);
  not not_37 (not_37_out, A6);
  not not_38 (not_38_out, A7);
  not not_39 (not_39_out, A5);
  not not_40 (not_40_out, A7);
  not not_41 (not_41_out, A4);
  not not_42 (not_42_out, A3);
  not not_43 (not_43_out, A2);
  and and_2 (and_2_out, A7, A6, A3);
  and and_3 (and_3_out, A7, A6, A4);
  and and_4 (and_4_out, A7, A6, A5);
  and and_5 (and_5_out, not_1_out, not_2_out);
  and and_6 (and_6_out, not_3_out, not_4_out);
  and and_7 (and_7_out, not_5_out, not_6_out, not_7_out, not_8_out);
  and and_8 (and_8_out, A6, not_9_out, A3);
  and and_9 (and_9_out, A6, not_10_out, A4);
  and and_10 (and_10_out, A7, A6, A5);
  or or_1 (C, not_11_out, not_12_out, and_1_out);
  and and_11 (and_11_out, not_16_out, not_17_out);
  and and_12 (and_12_out, not_18_out, not_19_out);
  and and_13 (and_13_out, not_20_out, not_21_out, not_22_out, not_23_out);
  and and_14 (and_14_out, A6, not_24_out, A3);
  and and_15 (and_15_out, A6, not_25_out, A4);
  and and_16 (and_16_out, A7, A6, A5);
  and and_17 (and_17_out, not_26_out, not_27_out);
  and and_18 (and_18_out, not_28_out, not_29_out);
  and and_19 (and_19_out, not_30_out, not_31_out, not_32_out, not_33_out);
  and and_20 (and_20_out, A6, not_34_out, A3);
  and and_21 (and_21_out, A6, not_35_out, A4);
  and and_22 (and_22_out, A7, A6, A5);
  and and_23 (and_23_out, not_36_out, not_37_out);
  or or_2 (F, and_23_out, and_24_out, and_25_out);
  and and_24 (and_24_out, not_38_out, not_39_out);
  and and_25 (and_25_out, not_40_out, not_41_out, not_42_out, not_43_out);
  or or_3 (G, and_2_out, and_3_out, and_4_out);
  or or_4 (A, and_5_out, and_6_out, and_7_out, and_8_out, and_9_out, and_10_out);
  or or_5 (D, and_11_out, and_12_out, and_13_out, and_14_out, and_15_out, and_16_out);
  or or_6 (E, and_17_out, and_18_out, and_19_out, and_20_out, and_21_out, and_22_out);

  assign B = 1'b1;

  // Notes on the sheet:
  //   DISPLAY UNIDADE
endmodule

module Mux4x1 (
  input  SOMA,
  input  \SUBTRAÇÃO ,
  input  \MULTIPLICAÇÃO ,
  input  \DIVISÃO ,
  input  in_5,
  input  in_6,
  output out_7
);

  wire and_1_out, and_2_out, and_3_out, and_4_out;

  and and_1 (and_1_out, SOMA, ~in_5, ~in_6);  // AND_Gate
  and and_2 (and_2_out, \SUBTRAÇÃO , ~in_5, in_6);  // AND_Gate
  and and_3 (and_3_out, \MULTIPLICAÇÃO , in_5, ~in_6);  // AND_Gate
  and and_4 (and_4_out, \DIVISÃO , in_5, in_6);
  or or_1 (out_7, and_1_out, and_2_out, and_3_out, and_4_out);

  // Notes on the sheet:
  //   MUX 4X1
endmodule

module Mux_4x1___8bits (
  input  [7:0] in_1,
  input  [7:0] in_2,
  input  [7:0] in_3,
  input  [7:0] in_4,
  input  [1:0] in_5,
  output [7:0] out_6
);

  Mux4x1 mux4x1_1 (
    .SOMA(in_1[0]), .\SUBTRAÇÃO (in_2[0]), .\MULTIPLICAÇÃO (in_3[0]), .\DIVISÃO (in_4[0]), .in_5(in_5[1]),
    .in_6(in_5[0]), .out_7(out_6[0]));
  Mux4x1 mux4x1_2 (
    .SOMA(in_1[1]), .\SUBTRAÇÃO (in_2[1]), .\MULTIPLICAÇÃO (in_3[1]), .\DIVISÃO (in_4[1]), .in_5(in_5[1]),
    .in_6(in_5[0]), .out_7(out_6[1]));
  Mux4x1 mux4x1_3 (
    .SOMA(in_1[2]), .\SUBTRAÇÃO (in_2[2]), .\MULTIPLICAÇÃO (in_3[2]), .\DIVISÃO (in_4[2]), .in_5(in_5[1]),
    .in_6(in_5[0]), .out_7(out_6[2]));
  Mux4x1 mux4x1_4 (
    .SOMA(in_1[3]), .\SUBTRAÇÃO (in_2[3]), .\MULTIPLICAÇÃO (in_3[3]), .\DIVISÃO (in_4[3]), .in_5(in_5[1]),
    .in_6(in_5[0]), .out_7(out_6[3]));
  Mux4x1 mux4x1_5 (
    .SOMA(in_1[4]), .\SUBTRAÇÃO (in_2[4]), .\MULTIPLICAÇÃO (in_3[4]), .\DIVISÃO (in_4[4]), .in_5(in_5[1]),
    .in_6(in_5[0]), .out_7(out_6[4]));
  Mux4x1 mux4x1_6 (
    .SOMA(in_1[5]), .\SUBTRAÇÃO (in_2[5]), .\MULTIPLICAÇÃO (in_3[5]), .\DIVISÃO (in_4[5]), .in_5(in_5[1]),
    .in_6(in_5[0]), .out_7(out_6[5]));
  Mux4x1 mux4x1_7 (
    .SOMA(in_1[6]), .\SUBTRAÇÃO (in_2[6]), .\MULTIPLICAÇÃO (in_3[6]), .\DIVISÃO (in_4[6]), .in_5(in_5[1]),
    .in_6(in_5[0]), .out_7(out_6[6]));
  Mux4x1 mux4x1_8 (
    .SOMA(in_1[7]), .\SUBTRAÇÃO (in_2[7]), .\MULTIPLICAÇÃO (in_3[7]), .\DIVISÃO (in_4[7]), .in_5(in_5[1]),
    .in_6(in_5[0]), .out_7(out_6[7]));

  // Notes on the sheet:
  //   SOMA
  //   MUX 4X1 - 8 BITS
  //   SUBTRAÇÃO
  //   MULTIPLICAÇÃO
  //   DIVISÃO
endmodule

module Comparador (
  input  [1:0] Chave_seletora,
  input  [3:0] Entrada_B,
  output sLed
);

  wire not_1_out, not_2_out, not_3_out, not_4_out;

  not not_1 (not_1_out, Entrada_B[0]);
  not not_2 (not_2_out, Entrada_B[1]);
  not not_3 (not_3_out, Entrada_B[2]);
  not not_4 (not_4_out, Entrada_B[3]);
  and and_1 (sLed, Chave_seletora[1], Chave_seletora[0], not_1_out, not_2_out, not_3_out, not_4_out);

  // Notes on the sheet:
  //   COMPARADOR
endmodule
